// Logisim project CS1409_U201414816_曾圳_cpu.circ as structural Verilog: 13 circuits, main circuit controller
module main (
);

  wire alu_1_equal, and_1_out, beq, bne, branch, clk, clock_1_out, comparator_1_eq, controller_1_jal,
       controller_1_mem_write, halt, id_ex_1_alu_src, id_ex_1_bltz_ctr, id_ex_1_data_src, jr, jump, load_use,
       Mem__EX_X, Mem__EX_Y, mem_read, mem_read_EX, mem_wb_1_jal, mem_wb_1_lbu, mem_wb_1_mem_reg,
       mem_wb_1_reg_write, mem_write_EX, mem_write_Mem, not_1_out, not_2_out, not_3_out, or_1_out, or_2_out,
       reg_dst_EX, reg_dst_ID, reg_dst_Mem, register_3_q, s_src, syscall, Wb__EX_R2, Wb__EX_X, Wb__EX_Y,
       Wb__ID_R1, Wb__ID_R2, Wb__Mem;
  wire [1:0] mem_wb_1_lbu_choose_2;
  wire [3:0] controller_1_alu_op, id_ex_1_alu_op_2;
  wire [4:0] ex_mem_1_rs_2, id_ex_1_rd_2, id_ex_1_s_2, id_ex_1_w_num_2, instruction_translate_1_rd_11_15,
       instruction_translate_1_s_6_10, multiplexer_3_out, multiplexer_6_out, multiplexer_7_out, rd_Mem,
       rs_EX, rs_ID, rt_EX, rt_ID, rt_Mem, W__Mem, W__Wb;
  wire [8:0] demultiplexer_1_out0, demultiplexer_1_out1;
  wire [9:0] shifter_3_out;
  wire [13:0] ex_mem_1_control_2;
  wire [15:0] id_ex_1_control_2, id_ex_1_imm_offset_2, instruction_translate_1_imm_0_15;
  wire [23:0] controller_1_control;
  wire [31:0] a0, adder_1_out, adder_2_out, adder_3_out, adder_5_out, adder_6_out, alu_1_result, and_2_out,
       b_count, bit_extender_1_out, bit_extender_2_out, bit_extender_3_out, count, data, ex_mem_1_r2_2,
       id_ex_1_r1_2, id_ex_1_r2_2, IR1, IR2, IR3, IR4, IR5, j_count, l_u_count, mem_wb_1_data_2,
       mem_wb_1_r2_2, \mips寄存器组_1_r1 , \mips寄存器组_1_r2 , multiplexer_4_out, multiplexer_5_out,
       multiplexer_8_out, multiplexer_9_out, multiplexer_10_out, multiplexer_11_out, multiplexer_12_out,
       multiplexer_13_out, multiplexer_14_out, multiplexer_15_out, multiplexer_16_out, multiplexer_17_out,
       multiplexer_19_out, multiplexer_20_out, multiplexer_21_out, multiplexer_22_out, multiplexer_23_out,
       multiplexer_25_out, pc1, pc2, pc3, pc4, pc5, pc_4, R_Mem, R_Wb, ram_1_data, register_1_q,
       register_6_q, rom_1_data, rom_2_data, s0, s1, s2, s3, shifter_1_out, shifter_2_out, v0;

  not not_1 (not_1_out, load_use);
  Demultiplexer #(.width(9)) demultiplexer_1 (
    .out0(demultiplexer_1_out0), .out1(demultiplexer_1_out1), .in(register_1_q[10:2]), .sel(1'b0), .en(1'b1));
  Register #(.width(32)) register_1 (.D(pc_4), .en(not_1_out), .Q(register_1_q), .clk(clk), .clr(1'b0));
  Register #(.width(32)) register_2 (.D(adder_2_out), .en(load_use), .Q(l_u_count), .clk(clk));  // open: clr
  Register #(.width(1)) register_3 (.D(halt), .en(1'b1), .Q(register_3_q), .clk(clk));  // open: clr
  // Probe on b_count
  Register #(.width(32)) register_4 (.D(adder_1_out), .en(branch), .Q(b_count), .clk(clk));  // open: clr
  or or_1 (or_1_out, jump, jr);
  Clock clock_1 (.out(clock_1_out));
  Multiplexer #(.enable("false")) multiplexer_1 (.in0(clock_1_out), .in1(1'b1), .out(clk), .sel(register_3_q));
  and and_1 (and_1_out, syscall, not_2_out);
  not not_2 (not_2_out, halt);
  Adder #(.width(32)) adder_1 (.a(b_count), .b(32'h1), .out(adder_1_out));  // open: cin, cout
  Register #(.width(32)) register_5 (.D(adder_3_out), .en(or_1_out), .Q(j_count), .clk(clk));  // open: clr
  Adder #(.width(32)) adder_2 (.a(l_u_count), .b(32'h1), .out(adder_2_out));  // open: cin, cout
  Hex_Digit_Display hex_digit_display_1 (.value(register_6_q[31:28]));  // open: dp
  Hex_Digit_Display hex_digit_display_2 (.value(register_6_q[27:24]));  // open: dp
  Register #(.width(32)) register_6 (.D(a0), .en(and_1_out), .Q(register_6_q), .clk(clk), .clr(1'b0));
  // Probe on l_u_count
  Adder #(.width(32)) adder_3 (.a(j_count), .b(32'h1), .out(adder_3_out));  // open: cin, cout
  Adder #(.width(32)) adder_4 (.a(register_1_q), .b(32'h4), .out(pc1), .cin(1'b0));  // open: cout
  ROM #(.addrWidth(9), .dataWidth(32)) rom_1 (.addr(demultiplexer_1_out0), .data(rom_1_data), .sel(1'b1));
  Multiplexer #(.width(32)) multiplexer_2 (.in0(rom_1_data), .in1(rom_2_data), .out(IR1), .sel(1'b0), .en(1'b1));
  ROM #(.addrWidth(9), .dataWidth(32)) rom_2 (.addr(demultiplexer_1_out1), .data(rom_2_data), .sel(1'b1));
  or or_2 (or_2_out, branch, jump, jr);
  Hex_Digit_Display hex_digit_display_3 (.value(register_6_q[19:16]));  // open: dp
  Hex_Digit_Display hex_digit_display_4 (.value(register_6_q[23:20]));  // open: dp
  Register #(.width(32)) register_7 (.D(adder_5_out), .en(1'b1), .Q(count), .clk(clk), .clr(1'b0));
  // Probe on count
  // Probe on j_count
  IF_ID if_id_1 (
    .clk(clk), .pc(pc1), .instruction(IR1), .enable(not_3_out), .clear(or_2_out), .new_pc(pc2),
    .new_instruction(IR2));
  not not_3 (not_3_out, load_use);
  Hex_Digit_Display hex_digit_display_5 (.value(register_6_q[15:12]));  // open: dp
  Hex_Digit_Display hex_digit_display_6 (.value(register_6_q[11:8]));  // open: dp
  Adder #(.width(32)) adder_5 (.a(count), .b(32'h1), .out(adder_5_out));  // open: cin, cout
  Hex_Digit_Display hex_digit_display_7 (.value(register_6_q[7:4]));  // open: dp
  Hex_Digit_Display hex_digit_display_8 (.value(register_6_q[3:0]));  // open: dp
  controller controller_1 (
    .alu_op(controller_1_alu_op), .reg_dst(reg_dst_ID), .mem_write(controller_1_mem_write),
    .instruction(IR2), .jal(controller_1_jal), .control(controller_1_control));  // open: branch_ne, jump, reg_write, mem_read, alu_src, mem_reg, branch_eq, mem_count, other_count, lbu, syacall, jr, s_src, data_src, alu_count, jump_count, branch_count, bltz_ctr, eret, cp0_write, mfc0
  instruction_translate instruction_translate_1 (
    .instruction(IR2), .rs_21_25(rs_ID), .imm_0_15(instruction_translate_1_imm_0_15),
    .rd_11_15(instruction_translate_1_rd_11_15), .rt_16_20(rt_ID), .s_6_10(instruction_translate_1_s_6_10));  // open: func_0_5, op_26_31, offset_0_15, instr_index_0_25
  // Probe on pc1
  // Probe on pc2
  // Probe on pc3
  // Probe on pc4
  // Probe on pc5
  // Probe on pc_4
  \MIPS寄存器组  \mips寄存器组_1  (
    .W_num(W__Wb), .Din(data), .WE(mem_wb_1_reg_write), .R2_num(rt_ID), .R1_num(rs_ID), .s0(s0), .s1(s1),
    .s2(s2), .R1(\mips寄存器组_1_r1 ), .R2(\mips寄存器组_1_r2 ), .clk(clk), .v0(v0), .s3(s3), .a0(a0));  // open: ra, s4
  Multiplexer #(.width(5), .enable("false")) multiplexer_3 (
    .in0(rt_ID), .in1(instruction_translate_1_rd_11_15), .out(multiplexer_3_out), .sel(reg_dst_ID));
  // Probe on IR1
  // Probe on IR2
  // Probe on IR3
  // Probe on IR4
  // Probe on IR5
  Multiplexer #(.width(32), .enable("false")) multiplexer_4 (
    .in0(\mips寄存器组_1_r1 ), .in1(data), .out(multiplexer_4_out), .sel(Wb__ID_R1));
  Multiplexer #(.width(32), .enable("false")) multiplexer_5 (
    .in0(\mips寄存器组_1_r2 ), .in1(data), .out(multiplexer_5_out), .sel(Wb__ID_R2));
  Multiplexer #(.width(5), .enable("false")) multiplexer_6 (
    .in0(multiplexer_3_out), .in1({5{1'b1}}), .out(multiplexer_6_out), .sel(controller_1_jal));
  Multiplexer #(.width(5), .enable("false")) multiplexer_7 (
    .in0(multiplexer_6_out), .in1({5{1'b0}}), .out(multiplexer_7_out), .sel(controller_1_mem_write));
  ID_EX id_ex_1 (
    .W_num(multiplexer_7_out), .imm_offset(instruction_translate_1_imm_0_15), .pc_4(pc2),
    .R1(multiplexer_4_out), .R2(multiplexer_5_out), .rs(rs_ID), .rd(instruction_translate_1_rd_11_15),
    .clk(clk), .control(controller_1_control), .IR(IR2), .rt(rt_ID), .alu_op(controller_1_alu_op),
    .s(instruction_translate_1_s_6_10), .W_num_2(id_ex_1_w_num_2), .rs_2(rs_EX),
    .imm_offset_2(id_ex_1_imm_offset_2), .rt_2(rt_EX), .pc_4_2(pc3), .rd_2(id_ex_1_rd_2),
    .R1_2(id_ex_1_r1_2), .alu_op_2(id_ex_1_alu_op_2), .R2_2(id_ex_1_r2_2), .control_2(id_ex_1_control_2),
    .IR_2(IR3), .s_2(id_ex_1_s_2), .data_src(id_ex_1_data_src), .alu_src(id_ex_1_alu_src), .s_src(s_src),
    .bltz_ctr(id_ex_1_bltz_ctr), .mem_read_EX(mem_read_EX), .load_use(load_use), .reg_dst_EX(reg_dst_EX),
    .mem_write_EX(mem_write_EX), .jump(jump), .jr(jr), .bne(bne), .beq(beq), .clear(or_2_out));
  // Probe on s0
  // Probe on s1
  // Probe on s2
  // Probe on s3
  // Probe on v0
  // Probe on a0
  Shifter #(.width(32)) shifter_1 (.in(IR3), .\dist (5'b00010), .out(shifter_1_out));
  assign bit_extender_1_out = {{16{id_ex_1_imm_offset_2[15]}}, id_ex_1_imm_offset_2};  // Bit_Extender bit_extender_1
  assign bit_extender_2_out = {{16{1'b0}}, id_ex_1_imm_offset_2};  // Bit_Extender bit_extender_2
  assign bit_extender_3_out = {{27{1'b0}}, id_ex_1_s_2};  // Bit_Extender bit_extender_3
  Shifter #(.width(32)) shifter_2 (.in(bit_extender_1_out), .\dist (5'b00010), .out(shifter_2_out));
  Multiplexer #(.width(32), .enable("false")) multiplexer_8 (
    .in0(bit_extender_1_out), .in1(bit_extender_2_out), .out(multiplexer_8_out), .sel(id_ex_1_data_src));
  Adder #(.width(32)) adder_6 (.a(pc3), .b(shifter_2_out), .out(adder_6_out), .cin(1'b0));  // open: cout
  branch branch_1 (
    .branch_ne(bne), .equal(alu_1_equal), .R(alu_1_result[0]), .branch_eq(beq), .bltz_ctr(id_ex_1_bltz_ctr),
    .branch(branch));
  Multiplexer #(.width(32), .enable("false")) multiplexer_9 (
    .in0(id_ex_1_r2_2), .in1(multiplexer_8_out), .out(multiplexer_9_out), .sel(id_ex_1_alu_src));
  Multiplexer #(.width(32), .enable("false")) multiplexer_10 (
    .in0(multiplexer_9_out), .in1(bit_extender_3_out), .out(multiplexer_10_out), .sel(s_src));
  Multiplexer #(.width(32), .enable("false")) multiplexer_11 (
    .in0(id_ex_1_r1_2), .in1(id_ex_1_r2_2), .out(multiplexer_11_out), .sel(s_src));
  Multiplexer #(.width(32), .enable("false")) multiplexer_12 (
    .in0(multiplexer_10_out), .in1({32{1'b0}}), .out(multiplexer_12_out), .sel(id_ex_1_bltz_ctr));
  Multiplexer #(.width(32), .enable("false")) multiplexer_13 (
    .in0(multiplexer_14_out), .in1({pc3[31:28], shifter_1_out[27:0]}), .out(multiplexer_13_out), .sel(jump));
  Multiplexer #(.width(32), .enable("false")) multiplexer_14 (
    .in0(pc1), .in1(adder_6_out), .out(multiplexer_14_out), .sel(branch));
  Multiplexer #(.width(32), .enable("false")) multiplexer_15 (
    .in0(multiplexer_11_out), .in1(data), .out(multiplexer_15_out), .sel(Wb__EX_X));
  Multiplexer #(.width(32), .enable("false")) multiplexer_16 (
    .in0(multiplexer_12_out), .in1(data), .out(multiplexer_16_out), .sel(Wb__EX_Y));
  Multiplexer #(.width(32), .enable("false")) multiplexer_17 (
    .in0(id_ex_1_r2_2), .in1(data), .out(multiplexer_17_out), .sel(Wb__EX_R2));
  \data重定向机制  \data重定向机制_1  (
    .rs_EX(rs_EX), .W__Mem(W__Mem), .mem_write_EX(mem_write_EX), .reg_dst_EX(reg_dst_EX), .rt_EX(rt_EX),
    .W__Wb(W__Wb), .mem_write_Mem(mem_write_Mem), .rt_Mem(rt_Mem), .s_src(s_src), .Mem__EX_X(Mem__EX_X),
    .Mem__EX_Y(Mem__EX_Y), .Wb__EX_X(Wb__EX_X), .Wb__EX_Y(Wb__EX_Y), .Wb__Mem(Wb__Mem),
    .Wb__EX_R2(Wb__EX_R2), .reg_dst_ID(reg_dst_ID), .Wb__ID_R1(Wb__ID_R1), .Wb__ID_R2(Wb__ID_R2),
    .rs_ID(rs_ID), .rt_ID(rt_ID), .bne(bne), .beq(beq));
  Multiplexer #(.width(32), .enable("false")) multiplexer_18 (
    .in0(multiplexer_13_out), .in1(multiplexer_19_out), .out(pc_4), .sel(jr));
  Multiplexer #(.width(32), .enable("false")) multiplexer_19 (
    .in0(multiplexer_15_out), .in1(R_Mem), .out(multiplexer_19_out), .sel(Mem__EX_X));
  ALU alu_1 (
    .AluOP(id_ex_1_alu_op_2), .X(multiplexer_19_out), .Equal(alu_1_equal), .Result(alu_1_result),
    .Y(multiplexer_20_out));  // open: Signed_Overflow, Result_2, UnSigned_Overflow
  Multiplexer #(.width(32), .enable("false")) multiplexer_20 (
    .in0(multiplexer_16_out), .in1(R_Mem), .out(multiplexer_20_out), .sel(Mem__EX_Y));
  EX_Mem ex_mem_1 (
    .pc_4(pc3), .IR(IR3), .control(id_ex_1_control_2), .clk(clk), .R(alu_1_result), .R2(multiplexer_17_out),
    .pc(pc4), .IR_2(IR4), .control_2(ex_mem_1_control_2), .R_2(R_Mem), .R2_2(ex_mem_1_r2_2),
    .mem_write(mem_write_Mem), .mem_read(mem_read), .rt(rt_EX), .rd(id_ex_1_rd_2), .rt_2(rt_Mem),
    .rd_2(rd_Mem), .rs(rs_EX), .rs_2(ex_mem_1_rs_2), .W_num(id_ex_1_w_num_2), .W_num_2(W__Mem),
    .reg_dst_Mem(reg_dst_Mem));
  \load_use检测  \load_use检测_1  (
    .rs_ID(rs_ID), .mem_read(mem_read_EX), .rt_ID(rt_ID), .rt_EX(rt_EX), .load_use(load_use));
  Shifter #(.width(10), .shift("lr")) shifter_3 (.in(R_Mem[9:0]), .\dist (4'b0010), .out(shifter_3_out));
  Multiplexer #(.width(32), .enable("false")) multiplexer_21 (
    .in0(ex_mem_1_r2_2), .in1(R_Wb), .out(multiplexer_21_out), .sel(Wb__Mem));
  RAM #(.addrWidth(10), .dataWidth(32), .bus("separate")) ram_1 (
    .addr(shifter_3_out), .din(multiplexer_21_out), .data(ram_1_data), .str(mem_write_Mem), .sel(1'b1),
    .clk(clk), .ld(mem_read), .clr(1'b0));
  Mem_Wb mem_wb_1 (
    .pc_4(pc4), .IR(IR4), .control(ex_mem_1_control_2), .clk(clk), .R(R_Mem), .data(ram_1_data),
    .syscall(syscall), .mem_reg(mem_wb_1_mem_reg), .pc(pc5), .jal(mem_wb_1_jal),
    .reg_write(mem_wb_1_reg_write), .IR_2(IR5), .lbu(mem_wb_1_lbu), .R_2(R_Wb), .data_2(mem_wb_1_data_2),
    .rt(rt_Mem), .rd(rd_Mem), .rs(ex_mem_1_rs_2), .W_num(W__Mem), .W_num_2(W__Wb), .R2(ex_mem_1_r2_2),
    .R2_2(mem_wb_1_r2_2), .lbu_choose(R_Mem[1:0]), .lbu_choose_2(mem_wb_1_lbu_choose_2));  // open: clear, reg_dst, alu_count, jump_count, branch_count, mem_count, other_count, rt_2, rd_2, rs_2
  Multiplexer #(.select(2), .width(32), .enable("false")) multiplexer_22 (
    .in0(32'hff), .in1(32'hff00), .in2(32'hff0000), .in3(32'hff000000), .out(multiplexer_22_out),
    .sel(mem_wb_1_lbu_choose_2));
  assign and_2_out = multiplexer_22_out & mem_wb_1_data_2;  // AND_Gate and_2, 32 bits wide
  Multiplexer #(.width(32), .enable("false")) multiplexer_23 (
    .in0(mem_wb_1_data_2), .in1(R_Wb), .out(multiplexer_23_out), .sel(mem_wb_1_mem_reg));
  Multiplexer #(.width(32), .enable("false")) multiplexer_24 (
    .in0(mem_wb_1_r2_2), .in1(data), .sel(mem_wb_1_reg_write));  // open: out
  Multiplexer #(.width(32), .enable("false")) multiplexer_25 (
    .in0(multiplexer_23_out), .in1(pc5), .out(multiplexer_25_out), .sel(mem_wb_1_jal));
  Comparator #(.width(32)) comparator_1 (.a(32'ha), .b(v0), .eq(comparator_1_eq));  // open: gt, lt
  Multiplexer #(.width(32), .enable("false")) multiplexer_26 (
    .in0(multiplexer_25_out), .in1(and_2_out), .out(data), .sel(mem_wb_1_lbu));
  and and_3 (halt, syscall, comparator_1_eq);

  // Other names for the same wires on the sheet: data1[31:0] = data

  // Notes on the sheet:
  //   contents of rom_1 (hex, n*v repeats v):
  //   20110001 8000c05 20110001 20120002 20130003 8000c09 20110001 20120002 20130003 8000c0d 20110001
  //   20120002 20130003 8000c11 20110001 20120002 20130003 c000cb8 20100001 20110001 118fc0 112020
  //   20020022 c 118882 12200001 8000c15 112020 20020022 c 20110001 118880 112020 20020022 c 12200001
  //   8000c1f 20110001 118fc0 112020 20020022 c 1188c3 112020 20020022 c 118903 112020 20020022 c 118903
  //   112020 20020022 c 118903 112020 20020022 c 118903 112020 20020022 c 118903 112020 20020022 c 118903
  //   112020 20020022 c 118903 112020 20020022 c 20100001 109fc0 139fc3 8021 2012000c 24160003 26100001
  //   3210000f 20080008 20090001 139900 2709825 132020 20020022 c 1094022 1500fff9 22100001 2018000f
  //   2188024 108700 20080008 20090001 139902 2709825 132021 20020022 c 1094022 1500fff9 108702 2c9b022
  //   12c00001 8000c50 4020 1084027 84400 3508ffff 82021 20020022 c 2010ffff 20110000 ae300000 22100001
  //   22310004 ae300000 22100001 22310004 ae300000 22100001 22310004 ae300000 22100001 22310004 ae300000
  //   22100001 22310004 ae300000 22100001 22310004 ae300000 22100001 22310004 ae300000 22100001 22310004
  //   ae300000 22100001 22310004 ae300000 22100001 22310004 ae300000 22100001 22310004 ae300000 22100001
  //   22310004 ae300000 22100001 22310004 ae300000 22100001 22310004 ae300000 22100001 22310004 ae300000
  //   22100001 22310004 22100001 8020 2011003c 8e130000 8e340000 274402a 11000002 ae330000 ae140000
  //   2231fffc 1611fff8 102020 20020022 c 22100004 2011003c 1611fff2 2002000a c 20100000 22100001 102020
  //   20020022 c 22100002 102020 20020022 c 22100003 102020 20020022 c 22100004 102020 20020022 c 22100005
  //   102020 20020022 c 22100006 102020 20020022 c 22100007 102020 20020022 c 22100008 102020 20020022
  //   20020022 c 3e00008
endmodule

module controller (
  input  [31:0] instruction,
  output [3:0] alu_op,
  output reg_dst,
  output jump,
  output bltz_ctr,
  output jal,
  output alu_count,
  output mfc0,
  output mem_write,
  output jr,
  output mem_reg,
  output s_src,
  output jump_count,
  output cp0_write,
  output [23:0] control,
  output mem_read,
  output branch_ne,
  output syacall,
  output data_src,
  output branch_count,
  output eret,
  output reg_write,
  output branch_eq,
  output alu_src,
  output lbu,
  output mem_count,
  output other_count
);

  wire add, addi, addiu, addu, alu_count_out, alu_src_out, \and , and_14_out, andi, eret_3_out, eret_out, j,
       lw, mem_reg_3_out, mem_reg_out, mfc0_3_out, mfc0_out, mtc0, \nor , op, \or , or_1_out, or_2_out,
       or_3_out, or_5_out, ori, reg_dst_out, reg_write_2_out, reg_write_3_out, reg_write_out, sll, slt, slti,
       sltiu, sltu, sra, srl, sub, \xor ;
  wire [3:0] and_1_out, and_2_out, and_3_out, and_4_out, and_5_out, and_6_out, and_7_out, and_9_out,
       and_10_out, and_11_out, and_12_out, and_13_out, bit_extender_1_out, bit_extender_2_out,
       bit_extender_3_out, bit_extender_4_out, bit_extender_5_out, bit_extender_6_out, bit_extender_7_out,
       bit_extender_8_out, bit_extender_9_out, bit_extender_10_out, bit_extender_11_out, bit_extender_12_out,
       or_4_out, or_7_out;
  wire [4:0] not_3_out, not_4_out;
  wire [5:0] not_1_out, not_2_out;

  assign not_1_out = ~instruction[31:26];  // NOT_Gate not_1, 6 bits wide
  assign not_2_out = ~instruction[5:0];  // NOT_Gate not_2, 6 bits wide
  and u_op (op, not_1_out[0], not_1_out[1], not_1_out[2], not_1_out[3], not_1_out[4], not_1_out[5]);
  and u_add (add, not_2_out[4], not_2_out[3], not_2_out[2], not_2_out[1], not_2_out[0], instruction[5], op);
  or or_1 (or_1_out, control[15], add, addiu, addi, control[8], lw, addu);
  assign bit_extender_1_out = {{3{or_1_out}}, or_1_out};  // Bit_Extender bit_extender_1
  assign bit_extender_2_out = {{3{\xor }}, \xor };  // Bit_Extender bit_extender_2
  assign bit_extender_3_out = {{3{or_2_out}}, or_2_out};  // Bit_Extender bit_extender_3
  or or_2 (or_2_out, \and , andi);
  assign bit_extender_4_out = {{3{sll}}, sll};  // Bit_Extender bit_extender_4
  and u_lw (lw, instruction[26], instruction[27], instruction[31], not_1_out[2], not_1_out[3], not_1_out[4]);
  and u_addi (addi, instruction[29], not_1_out[0], not_1_out[1], not_1_out[2], not_1_out[4], not_1_out[5]);
  assign and_1_out = bit_extender_1_out & 4'b0101;  // AND_Gate and_1, 4 bits wide
  assign and_2_out = bit_extender_2_out & 4'b1001;  // AND_Gate and_2, 4 bits wide
  assign and_3_out = bit_extender_3_out & 4'b0111;  // AND_Gate and_3, 4 bits wide
  assign and_4_out = bit_extender_4_out & 4'b0000;  // AND_Gate and_4, 4 bits wide
  and sw (control[8], instruction[26], instruction[27], instruction[29], instruction[31], not_1_out[2], not_1_out[4]);
  and u_addiu (addiu, instruction[26], instruction[29], not_1_out[1], not_1_out[2], not_1_out[4], not_1_out[5]);
  assign bit_extender_5_out = {{3{sra}}, sra};  // Bit_Extender bit_extender_5
  assign bit_extender_6_out = {{3{srl}}, srl};  // Bit_Extender bit_extender_6
  assign bit_extender_7_out = {{3{\nor }}, \nor };  // Bit_Extender bit_extender_7
  and beq (branch_eq, instruction[28], not_1_out[0], not_1_out[1], not_1_out[3], not_1_out[4], not_1_out[5]);
  and u_addu (addu, instruction[0], instruction[5], not_2_out[1], not_2_out[2], not_2_out[3], not_2_out[4], op);
  or u_reg_dst (reg_dst_out, add, addu, \and , sll, sra, srl, sub, \or , \nor , slt, sltu);
  or reg_dst_2 (control[14], reg_dst_out, \xor );
  assign and_5_out = bit_extender_5_out & 4'b0001;  // AND_Gate and_5, 4 bits wide
  assign and_6_out = bit_extender_6_out & 4'b0010;  // AND_Gate and_6, 4 bits wide
  assign and_7_out = bit_extender_7_out & 4'b1010;  // AND_Gate and_7, 4 bits wide
  and and_8 (\and , instruction[2], instruction[5], not_2_out[0], not_2_out[1], not_2_out[3], not_2_out[4], op);
  and bne (branch_ne, instruction[26], instruction[28], not_1_out[1], not_1_out[3], not_1_out[4], not_1_out[5]);
  and u_andi (andi, instruction[28], instruction[29], not_1_out[0], not_1_out[1], not_1_out[4], not_1_out[5]);
  or u_jump (control[0], control[1], control[12], j);
  and u_slti (slti, instruction[27], instruction[29], not_1_out[0], not_1_out[2], not_1_out[4], not_1_out[5]);
  and u_sll (sll, not_2_out[0], not_2_out[1], not_2_out[2], not_2_out[3], not_2_out[4], not_2_out[5], op);
  or or_3 (or_3_out, sltu, sltiu);
  assign or_4_out = and_1_out | and_5_out | and_2_out | and_6_out | and_3_out | and_7_out | and_4_out;  // OR_Gate or_4, 4 bits wide
  or or_5 (or_5_out, slt, bltz_ctr, slti);
  and u_sra (sra, instruction[0], instruction[1], not_2_out[2], not_2_out[3], not_2_out[4], not_2_out[5], op);
  or u_reg_write (reg_write_out, add, addu, \and , sll, sra, srl, sub, \or , \nor , slt, sltu);
  assign bit_extender_8_out = {{3{or_3_out}}, or_3_out};  // Bit_Extender bit_extender_8
  assign and_9_out = bit_extender_8_out & 4'b1100;  // AND_Gate and_9, 4 bits wide
  assign bit_extender_9_out = {{3{or_5_out}}, or_5_out};  // Bit_Extender bit_extender_9
  and u_j (j, instruction[27], not_1_out[0], not_1_out[2], not_1_out[3], not_1_out[4], not_1_out[5]);
  and u_srl (srl, instruction[1], not_2_out[0], not_2_out[2], not_2_out[3], not_2_out[4], not_2_out[5], op);
  or reg_write_2 (reg_write_2_out, ori, andi, addi, control[12], addiu, slti, lw);
  or reg_write_3 (reg_write_3_out, reg_write_out, \xor , control[15], sltiu, reg_write_2_out);
  assign bit_extender_10_out = {{3{sub}}, sub};  // Bit_Extender bit_extender_10
  assign bit_extender_11_out = {{3{ori}}, ori};  // Bit_Extender bit_extender_11
  assign bit_extender_12_out = {{3{\or }}, \or };  // Bit_Extender bit_extender_12
  assign and_10_out = bit_extender_9_out & 4'b1011;  // AND_Gate and_10, 4 bits wide
  and u_jal (control[12], instruction[26], instruction[27], not_1_out[2], not_1_out[3], not_1_out[4], not_1_out[5]);
  and u_sub (sub, instruction[1], instruction[5], not_2_out[0], not_2_out[2], not_2_out[3], not_2_out[4], op);
  or reg_write_4 (control[13], reg_write_3_out, control[20]);
  assign and_11_out = bit_extender_10_out & 4'b0110;  // AND_Gate and_11, 4 bits wide
  assign and_12_out = bit_extender_11_out & 4'b1000;  // AND_Gate and_12, 4 bits wide
  assign and_13_out = bit_extender_12_out & 4'b1000;  // AND_Gate and_13, 4 bits wide
  and u_sltiu (sltiu, instruction[26], instruction[27], instruction[29], not_1_out[2], not_1_out[4], not_1_out[5]);
  and or_6 (\or , instruction[0], instruction[2], instruction[5], not_2_out[1], not_2_out[3], not_2_out[4], op);
  or u_mem_read (control[9], lw, control[15]);
  and u_lbu (control[15], instruction[28], instruction[31], not_1_out[0], not_1_out[1], not_1_out[3], not_1_out[4]);
  and u_ori (ori, instruction[26], instruction[28], instruction[29], not_1_out[1], not_1_out[4], not_1_out[5]);
  assign or_7_out = and_9_out | and_11_out | and_12_out | and_13_out | and_10_out;  // OR_Gate or_7, 4 bits wide
  and u_nor (\nor , instruction[0], instruction[1], instruction[2], instruction[5], not_2_out[3], not_2_out[4], op);
  or u_alu_src (alu_src_out, ori, andi, addi, lw, addiu, slti, control[8]);
  or alu_src_2 (alu_src, alu_src_out, control[15], sltiu);
  and bltz (bltz_ctr, instruction[26], not_1_out[1], not_1_out[2], not_1_out[3], not_1_out[4], not_1_out[5], and_14_out);
  and and_14 (and_14_out, not_3_out[4], not_3_out[3], not_3_out[2], not_3_out[1], not_3_out[0]);
  and u_slt (slt, instruction[1], instruction[3], instruction[5], not_2_out[0], not_2_out[2], not_2_out[4], op);
  or u_mem_reg (mem_reg_out, add, addu, \and , sll, sra, srl, sub, \or , \nor , slt, sltu);
  assign alu_op = or_4_out | or_7_out;  // OR_Gate or_8, 4 bits wide
  assign not_3_out = ~instruction[20:16];  // NOT_Gate not_3, 5 bits wide
  and u_sltu (sltu, instruction[0], instruction[1], instruction[3], instruction[5], not_2_out[2], not_2_out[4], op);
  or mem_reg_2 (control[11], mem_reg_out, \xor , sltiu, mem_reg_3_out);
  and u_jr (control[1], instruction[3], not_2_out[0], not_2_out[1], not_2_out[2], not_2_out[4], not_2_out[5], op);
  or mem_reg_3 (mem_reg_3_out, ori, andi, addi, addiu, slti);
  and u_eret (eret_out, instruction[30], not_1_out[0], not_1_out[1], not_1_out[2], not_1_out[3], not_1_out[5]);
  and syscall (control[10], instruction[2], instruction[3], not_2_out[0], not_2_out[1], not_2_out[4], not_2_out[5], op);
  and eret_2 (control[22], eret_out, eret_3_out);
  and eret_3 (eret_3_out, instruction[3], instruction[4], not_2_out[0], not_2_out[1], not_2_out[2], not_2_out[5]);
  and u_xor (\xor , instruction[5], instruction[1], instruction[2], not_2_out[3], not_2_out[0], not_2_out[4], op);
  and u_mfc0 (mfc0_out, instruction[30], not_1_out[0], not_1_out[1], not_1_out[2], not_1_out[3], not_1_out[5]);
  and mfc0_2 (control[20], mfc0_out, mfc0_3_out);
  or u_s_src (control[6], sll, srl, sra);
  and u_mtc0 (mtc0, mfc0_out, not_4_out[4], not_4_out[3], not_4_out[1], not_4_out[0], instruction[23]);
  and mfc0_3 (mfc0_3_out, not_4_out[4], not_4_out[3], not_4_out[2], not_4_out[1], not_4_out[0]);
  or u_data_src (control[4], andi, sltiu, ori);
  assign not_4_out = ~instruction[25:21];  // NOT_Gate not_4, 5 bits wide
  or u_alu_count (alu_count_out, add, \and , sll, sra, srl, sub, \or , \nor , ori, andi, addi, addiu, slti);
  or alu_count_2 (alu_count, alu_count_out, \xor , sltiu);
  or u_jump_count (control[17], control[1], control[12], j);
  or u_branch_count (branch_count, branch_eq, branch_ne);
  or u_mem_count (control[19], lw, control[15], control[8]);
  or u_other_count (control[23], sltu, slt, bltz_ctr, control[10], addu, control[22], control[20], mtc0);
  or mem_count_2 (control[21], control[22], mtc0);

  assign {control[18], control[16], control[7], control[5], control[3:2]} = {branch_count, alu_count, bltz_ctr, alu_src, branch_eq, branch_ne};
  assign cp0_write = control[21];
  assign data_src = control[4];
  assign eret = control[22];
  assign jal = control[12];
  assign jr = control[1];
  assign jump = control[0];
  assign jump_count = control[17];
  assign lbu = control[15];
  assign mem_count = control[19];
  assign mem_read = control[9];
  assign mem_reg = control[11];
  assign mem_write = control[8];
  assign mfc0 = control[20];
  assign other_count = control[23];
  assign reg_dst = control[14];
  assign reg_write = control[13];
  assign s_src = control[6];
  assign syacall = control[10];

  // Other names for the same wires on the sheet: control_1[7:0] = {bltz_ctr, control[6], alu_src, control[4], branch_eq, branch_ne, control[1:0]};
  //   bne = branch_ne; beq = branch_eq; bltz = bltz_ctr; control_2[7:0] = control[15:8]; sw = control[8];
  //   syscall = control[10]; control_3[7:0] = {control[23:19], branch_count, control[17], alu_count};
  //   func_0_5[5:0] = instruction[5:0]; bltz_16_20[4:0] = instruction[20:16];
  //   interrupt_21_25[4:0] = instruction[25:21]; op_26_31[5:0] = instruction[31:26]
endmodule

module counter (
  input  mem_count,
  input  alu_count,
  input  jump_count,
  input  branch_count,
  input  clk_count,
  input  other_count,
  output [11:0] mem_num,
  output [11:0] alu_num,
  output [11:0] jump_num,
  output [11:0] branch_num,
  output [11:0] clk_num,
  output [11:0] other_num
);

  wire [11:0] adder_1_out, adder_2_out, adder_3_out, adder_4_out, adder_5_out, adder_6_out;

  Register #(.width(12)) register_1 (.D(adder_1_out), .en(mem_count), .Q(mem_num), .clk(clk_count), .clr(1'b0));
  Register #(.width(12)) register_2 (.D(adder_2_out), .en(alu_count), .Q(alu_num), .clk(clk_count), .clr(1'b0));
  Register #(.width(12)) register_3 (.D(adder_3_out), .en(jump_count), .Q(jump_num), .clk(clk_count), .clr(1'b0));
  Register #(.width(12)) register_4 (.D(adder_4_out), .en(branch_count), .Q(branch_num), .clk(clk_count), .clr(1'b0));
  Register #(.width(12)) register_5 (.D(adder_5_out), .en(1'b1), .Q(clk_num), .clk(clk_count), .clr(1'b0));
  Register #(.width(12)) register_6 (.D(adder_6_out), .en(other_count), .Q(other_num), .clk(clk_count), .clr(1'b0));
  Adder #(.width(12)) adder_1 (.a(mem_num), .b(12'h1), .out(adder_1_out), .cin(1'b0));  // open: cout
  Adder #(.width(12)) adder_2 (.a(alu_num), .b(12'h1), .out(adder_2_out), .cin(1'b0));  // open: cout
  Adder #(.width(12)) adder_3 (.a(jump_num), .b(12'h1), .out(adder_3_out), .cin(1'b0));  // open: cout
  Adder #(.width(12)) adder_4 (.a(branch_num), .b(12'h1), .out(adder_4_out), .cin(1'b0));  // open: cout
  Adder #(.width(12)) adder_5 (.a(clk_num), .b(12'h1), .out(adder_5_out), .cin(1'b0));  // open: cout
  Adder #(.width(12)) adder_6 (.a(other_num), .b(12'h1), .out(adder_6_out), .cin(1'b0));  // open: cout
endmodule

module interrupt (
  input  clk,
  input  b_3,
  input  [31:0] status,
  input  [31:0] cause,
  input  b_1,
  input  eret,
  input  b_2,
  output [1:0] number,
  output _1,
  output _2,
  output _3,
  output interrupt
);

  wire and_2_out, and_3_out, and_4_out, c_1, c_2, c_3, IE_q, multiplexer_1_out, multiplexer_2_out,
       multiplexer_3_out, not_1_out, not_2_out, not_3_out, priority_encoder_1_gs, register_1_q, register_2_q,
       register_3_q, register_4_q, register_5_q, register_6_q, register_7_q, register_8_q, register_9_q,
       register_10_q;
  wire [1:0] priority_encoder_1_out;

  Register #(.width(1)) register_1 (.D(1'b1), .en(1'b1), .Q(register_1_q), .clk(b_1), .clr(c_1));
  Register #(.width(1)) register_2 (.D(1'b1), .en(1'b1), .Q(register_2_q), .clk(b_2), .clr(c_2));
  Register #(.width(1)) register_3 (.D(1'b1), .en(1'b1), .Q(register_3_q), .clk(b_3), .clr(c_3));
  not not_1 (not_1_out, register_4_q);
  Register #(.width(1)) register_4 (.D(status[1]), .en(1'b1), .Q(register_4_q), .clk(clk), .clr(1'b0));
  not not_2 (not_2_out, register_5_q);
  Register #(.width(1)) register_5 (.D(status[2]), .en(1'b1), .Q(register_5_q), .clk(clk), .clr(1'b0));
  Register #(.width(1)) register_6 (.D(status[3]), .en(1'b1), .Q(register_6_q), .clk(clk), .clr(1'b0));
  not not_3 (not_3_out, register_6_q);
  Register #(.width(1)) register_7 (.D(b_1), .en(1'b1), .Q(register_7_q), .clk(clk), .clr(1'b0));
  Multiplexer #(.enable("false")) multiplexer_1 (.in0(register_1_q), .in1(1'b0), .out(multiplexer_1_out), .sel(c_1));
  Multiplexer #(.enable("false")) multiplexer_2 (.in0(register_2_q), .in1(1'b0), .out(multiplexer_2_out), .sel(c_2));
  Multiplexer #(.enable("false")) multiplexer_3 (.in0(register_3_q), .in1(1'b0), .out(multiplexer_3_out), .sel(c_3));
  Register #(.width(1)) register_8 (.D(multiplexer_1_out), .en(1'b1), .Q(register_8_q), .clk(clk), .clr(1'b0));
  Register #(.width(1)) register_9 (.D(multiplexer_2_out), .en(1'b1), .Q(register_9_q), .clk(clk), .clr(1'b0));
  or or_1 (_2, register_9_q, register_2_q);
  or or_2 (_3, register_10_q, register_3_q);
  Register #(.width(1)) register_10 (.D(multiplexer_3_out), .en(1'b1), .Q(register_10_q), .clk(clk), .clr(1'b0));
  // AND_Gate and_1 has open pins: in0=register_7_q, in1=not_1_out, out=open
  or or_3 (_1, register_1_q, register_8_q);
  and and_2 (and_2_out, register_8_q, not_1_out);
  and and_3 (and_3_out, register_9_q, not_2_out);
  and and_4 (and_4_out, register_10_q, not_3_out);
  Register #(.width(1)) IE (.D(status[0]), .en(1'b1), .Q(IE_q), .clk(clk), .clr(1'b0));
  and and_5 (c_1, and_2_out, interrupt);
  and and_6 (c_2, and_3_out, interrupt);
  and and_7 (c_3, and_4_out, interrupt);
  Priority_Encoder #(.select(2)) priority_encoder_1 (
    .in0(1'b0), .in1(and_2_out), .in2(and_3_out), .in3(and_4_out), .out(priority_encoder_1_out),
    .gs(priority_encoder_1_gs), .en_in(1'b1));  // open: en_out
  and and_8 (interrupt, priority_encoder_1_gs, ~IE_q);  // AND_Gate
  // Probe on number
  Multiplexer #(.width(2)) multiplexer_4 (
    .in0(2'b00), .in1(priority_encoder_1_out), .out(number), .sel(priority_encoder_1_gs), .en(1'b1));

  // Other names for the same wires on the sheet: IE = status[0]; IP[2:0] = status[3:1]; change[1:0] = status[5:4]
endmodule

module cp0 (
  input  clk,
  input  WE,
  input  [4:0] W_num,
  input  [31:0] Din,
  input  [31:0] PC,
  input  [4:0] R_num,
  input  interrupt,
  output [31:0] epc,
  output [31:0] vaddr,
  output [31:0] status,
  output [31:0] cause,
  output [31:0] R
);

  wire demultiplexer_1_out8, demultiplexer_1_out12, demultiplexer_1_out13, demultiplexer_1_out14, or_1_out,
       or_2_out;
  wire [31:0] bit_extender_1_out, multiplexer_1_out, PC_buffer;

  Demultiplexer #(.select(5)) demultiplexer_1 (
    .out8(demultiplexer_1_out8), .out12(demultiplexer_1_out12), .out13(demultiplexer_1_out13),
    .out14(demultiplexer_1_out14), .in(WE), .sel(W_num), .en(1'b1));  // open: out0, out1, out2, out3, out4, out5, out6, out7, out9, out10, out11, out15, out16, out17, out18, out19, out20, out21, out22, out23, out24, out25, out26, out27, out28, out29, out30, out31
  or or_1 (or_1_out, demultiplexer_1_out13, interrupt);
  or or_2 (or_2_out, demultiplexer_1_out14, interrupt);
  Multiplexer #(.width(32)) multiplexer_1 (
    .in0(Din), .in1(PC_buffer), .out(multiplexer_1_out), .sel(interrupt), .en(1'b1));
  Register #(.width(32)) epc_buffer (.D(PC), .en(1'b1), .Q(PC_buffer), .clk(interrupt), .clr(1'b0));
  Register #(.width(32)) u_vaddr (.D(Din), .en(demultiplexer_1_out8), .Q(vaddr), .clk(clk), .clr(1'b0));
  Register #(.width(32)) u_status (.D(Din), .en(demultiplexer_1_out12), .Q(status), .clk(clk), .clr(1'b0));
  Register #(.width(32)) u_cause (.D(Din), .en(or_1_out), .Q(cause), .clk(clk), .clr(1'b0));
  Register #(.width(32)) u_epc (.D(multiplexer_1_out), .en(or_2_out), .Q(epc), .clk(clk), .clr(1'b0));
  assign bit_extender_1_out = {{31{1'b0}}, 1'b0};  // Bit_Extender bit_extender_1
  Multiplexer #(.select(5), .width(32)) multiplexer_2 (
    .in0(bit_extender_1_out), .in1(bit_extender_1_out), .in2(bit_extender_1_out), .in3(bit_extender_1_out),
    .in4(bit_extender_1_out), .in5(bit_extender_1_out), .in6(bit_extender_1_out), .in7(bit_extender_1_out),
    .in8(vaddr), .in9(bit_extender_1_out), .in10(bit_extender_1_out), .in11(bit_extender_1_out),
    .in12(status), .in13(cause), .in14(epc), .in15(bit_extender_1_out), .in16(bit_extender_1_out),
    .in17(bit_extender_1_out), .in18(bit_extender_1_out), .in19(bit_extender_1_out),
    .in20(bit_extender_1_out), .in21(bit_extender_1_out), .in22(bit_extender_1_out),
    .in23(bit_extender_1_out), .in24(bit_extender_1_out), .in25(bit_extender_1_out),
    .in26(bit_extender_1_out), .in27(bit_extender_1_out), .in28(bit_extender_1_out),
    .in29(bit_extender_1_out), .in30(bit_extender_1_out), .in31(bit_extender_1_out), .out(R), .sel(R_num),
    .en(1'b1));

  // Notes on the sheet:
  //   输入
  //   输出
endmodule

module IF_ID (
  input  clk,
  input  [31:0] pc,
  input  [31:0] instruction,
  input  enable,
  input  clear,
  output [31:0] new_pc,
  output [31:0] new_instruction
);

  wire [31:0] multiplexer_1_out, multiplexer_2_out;

  Multiplexer #(.width(32), .enable("false")) multiplexer_1 (
    .in0(pc), .in1({32{1'b0}}), .out(multiplexer_1_out), .sel(clear));
  Multiplexer #(.width(32), .enable("false")) multiplexer_2 (
    .in0(instruction), .in1({32{1'b0}}), .out(multiplexer_2_out), .sel(clear));
  Register #(.width(32)) register_1 (.D(multiplexer_1_out), .en(enable), .Q(new_pc), .clk(clk));  // open: clr
  Register #(.width(32)) register_2 (.D(multiplexer_2_out), .en(enable), .Q(new_instruction), .clk(clk));  // open: clr

  // Notes on the sheet:
  //   输入
  //   输出
endmodule

// translate
module instruction_translate (
  input  [31:0] instruction,
  output [5:0] func_0_5,
  output [4:0] rs_21_25,
  output [15:0] imm_0_15,
  output [4:0] rd_11_15,
  output [5:0] op_26_31,
  output [15:0] offset_0_15,
  output [4:0] rt_16_20,
  output [4:0] s_6_10,
  output [25:0] instr_index_0_25
);


  assign func_0_5 = instruction[5:0];
  assign imm_0_15 = instruction[15:0];
  assign instr_index_0_25 = instruction[25:0];
  assign offset_0_15 = instruction[15:0];
  assign op_26_31 = instruction[31:26];
  assign rd_11_15 = instruction[15:11];
  assign rs_21_25 = instruction[25:21];
  assign rt_16_20 = instruction[20:16];
  assign s_6_10 = instruction[10:6];

  // Other names for the same wires on the sheet: func[5:0] = instruction[5:0]; imm[15:0] = instruction[15:0];
  //   instr_index[25:0] = instruction[25:0]; offset[15:0] = instruction[15:0]; s[4:0] = instruction[10:6];
  //   rd[4:0] = instruction[15:11]; rt[4:0] = instruction[20:16]; rs[4:0] = instruction[25:21];
  //   op[5:0] = instruction[31:26]

  // Notes on the sheet:
  //   输入输出
endmodule

module ID_EX (
  input  [4:0] W_num,
  input  [15:0] imm_offset,
  input  [31:0] pc_4,
  input  [31:0] R1,
  input  [31:0] R2,
  input  [4:0] rs,
  input  [4:0] rd,
  input  clk,
  input  [23:0] control,
  input  [31:0] IR,
  input  [3:0] alu_op,
  input  [4:0] s,
  input  [4:0] rt,
  input  clear,
  input  load_use,
  output [4:0] W_num_2,
  output [4:0] rs_2,
  output [15:0] imm_offset_2,
  output [4:0] rt_2,
  output [31:0] pc_4_2,
  output [4:0] rd_2,
  output [31:0] R1_2,
  output [3:0] alu_op_2,
  output [4:0] s_2,
  output [31:0] R2_2,
  output beq,
  output bne,
  output jr,
  output jump,
  output data_src,
  output alu_src,
  output [31:0] IR_2,
  output s_src,
  output bltz_ctr,
  output mem_read_EX,
  output mem_write_EX,
  output [15:0] control_2,
  output reg_dst_EX
);

  wire or_1_out;
  wire [3:0] multiplexer_11_out;
  wire [4:0] multiplexer_1_out, multiplexer_8_out, multiplexer_9_out, multiplexer_10_out, multiplexer_12_out;
  wire [15:0] multiplexer_2_out;
  wire [23:0] multiplexer_6_out;
  wire [31:0] multiplexer_3_out, multiplexer_4_out, multiplexer_5_out, multiplexer_7_out;

  Multiplexer #(.width(5), .enable("false")) multiplexer_1 (
    .in0(W_num), .in1({5{1'b0}}), .out(multiplexer_1_out), .sel(or_1_out));
  Register #(.width(5)) register_1 (.D(multiplexer_1_out), .en(1'b1), .Q(W_num_2), .clk(clk));  // open: clr
  Multiplexer #(.width(16), .enable("false")) multiplexer_2 (
    .in0(imm_offset), .in1({16{1'b0}}), .out(multiplexer_2_out), .sel(or_1_out));
  Register #(.width(16)) register_2 (.D(multiplexer_2_out), .en(1'b1), .Q(imm_offset_2), .clk(clk));  // open: clr
  Multiplexer #(.width(32), .enable("false")) multiplexer_3 (
    .in0(pc_4), .in1({32{1'b0}}), .out(multiplexer_3_out), .sel(or_1_out));
  Register #(.width(32)) register_3 (.D(multiplexer_3_out), .en(1'b1), .Q(pc_4_2), .clk(clk));  // open: clr
  Multiplexer #(.width(32), .enable("false")) multiplexer_4 (
    .in0(R1), .in1({32{1'b0}}), .out(multiplexer_4_out), .sel(or_1_out));
  Register #(.width(32)) register_4 (.D(multiplexer_4_out), .en(1'b1), .Q(R1_2), .clk(clk));  // open: clr
  Multiplexer #(.width(32), .enable("false")) multiplexer_5 (
    .in0(R2), .in1({32{1'b0}}), .out(multiplexer_5_out), .sel(or_1_out));
  Register #(.width(32)) register_5 (.D(multiplexer_5_out), .en(1'b1), .Q(R2_2), .clk(clk));  // open: clr
  Multiplexer #(.width(24), .enable("false")) multiplexer_6 (
    .in0(control), .in1({24{1'b0}}), .out(multiplexer_6_out), .sel(or_1_out));
  Register #(.width(24)) register_6 (
    .D(multiplexer_6_out), .en(1'b1),
    .Q({control_2, bltz_ctr, s_src, alu_src, data_src, beq, bne, jr, jump}), .clk(clk));  // open: clr
  Multiplexer #(.width(32), .enable("false")) multiplexer_7 (
    .in0(IR), .in1({32{1'b0}}), .out(multiplexer_7_out), .sel(or_1_out));
  Register #(.width(32)) register_7 (.D(multiplexer_7_out), .en(1'b1), .Q(IR_2), .clk(clk));  // open: clr
  or or_1 (or_1_out, load_use, clear);
  Multiplexer #(.width(5), .enable("false")) multiplexer_8 (
    .in0(rs), .in1({5{1'b0}}), .out(multiplexer_8_out), .sel(or_1_out));
  Multiplexer #(.width(5), .enable("false")) multiplexer_9 (
    .in0(rt), .in1({5{1'b0}}), .out(multiplexer_9_out), .sel(or_1_out));
  Multiplexer #(.width(5), .enable("false")) multiplexer_10 (
    .in0(rd), .in1({5{1'b0}}), .out(multiplexer_10_out), .sel(or_1_out));
  Multiplexer #(.width(4), .enable("false")) multiplexer_11 (
    .in0(alu_op), .in1(4'b0000), .out(multiplexer_11_out), .sel(or_1_out));
  Multiplexer #(.width(5), .enable("false")) multiplexer_12 (
    .in0(s), .in1({5{1'b0}}), .out(multiplexer_12_out), .sel(or_1_out));
  Register #(.width(5)) register_8 (.D(multiplexer_8_out), .en(1'b1), .Q(rs_2), .clk(clk));  // open: clr
  Register #(.width(5)) register_9 (.D(multiplexer_9_out), .en(1'b1), .Q(rt_2), .clk(clk));  // open: clr
  Register #(.width(5)) register_10 (.D(multiplexer_10_out), .en(1'b1), .Q(rd_2), .clk(clk));  // open: clr
  Register #(.width(4)) register_11 (.D(multiplexer_11_out), .en(1'b1), .Q(alu_op_2), .clk(clk));  // open: clr
  Register #(.width(5)) register_12 (.D(multiplexer_12_out), .en(1'b1), .Q(s_2), .clk(clk));  // open: clr

  assign mem_read_EX = control_2[1];
  assign mem_write_EX = control_2[0];
  assign reg_dst_EX = control_2[6];

  // Notes on the sheet:
  //   输入
endmodule

module branch (
  input  branch_ne,
  input  equal,
  input  R,
  input  branch_eq,
  input  bltz_ctr,
  output branch
);

  wire and_1_out, and_2_out, and_3_out;

  and and_1 (and_1_out, ~equal, branch_ne);  // AND_Gate
  and and_2 (and_2_out, equal, branch_eq);
  and and_3 (and_3_out, bltz_ctr, R);
  Register #(.width(1)) register_1 (.D(1'b1), .clk(and_2_out));  // open: en, Q, clr
  or or_1 (branch, and_1_out, and_2_out, and_3_out);
  Register #(.width(1)) register_2 (.D(1'b1), .clk(branch));  // open: en, Q, clr

  // Notes on the sheet:
  //   input
endmodule

module EX_Mem (
  input  [31:0] pc_4,
  input  [31:0] IR,
  input  [15:0] control,
  input  [4:0] W_num,
  input  [4:0] rs,
  input  clk,
  input  [4:0] rt,
  input  [31:0] R,
  input  [31:0] R2,
  input  [4:0] rd,
  output [31:0] pc,
  output [31:0] IR_2,
  output mem_write,
  output mem_read,
  output reg_dst_Mem,
  output [31:0] R_2,
  output [13:0] control_2,
  output [31:0] R2_2,
  output [4:0] rt_2,
  output [4:0] rd_2,
  output [4:0] rs_2,
  output [4:0] W_num_2
);

  Register #(.width(32)) register_1 (.D(pc_4), .en(1'b1), .Q(pc), .clk(clk));  // open: clr
  Register #(.width(32)) register_2 (.D(IR), .en(1'b1), .Q(IR_2), .clk(clk));  // open: clr
  Register #(.width(16)) register_3 (
    .D(control), .en(1'b1), .Q({control_2, mem_read, mem_write}), .clk(clk));  // open: clr
  Register #(.width(32)) register_4 (.D(R), .en(1'b1), .Q(R_2), .clk(clk));  // open: clr
  Register #(.width(32)) register_5 (.D(R2), .en(1'b1), .Q(R2_2), .clk(clk));  // open: clr
  Register #(.width(5)) register_6 (.D(rt), .en(1'b1), .Q(rt_2), .clk(clk));  // open: clr
  Register #(.width(5)) register_7 (.D(rd), .en(1'b1), .Q(rd_2), .clk(clk));  // open: clr
  Register #(.width(5)) register_8 (.D(rs), .en(1'b1), .Q(rs_2), .clk(clk));  // open: clr
  Register #(.width(5)) register_9 (.D(W_num), .en(1'b1), .Q(W_num_2), .clk(clk));  // open: clr

  assign reg_dst_Mem = control_2[4];

  // Notes on the sheet:
  //   input
endmodule

module Mem_Wb (
  input  [31:0] pc_4,
  input  [31:0] IR,
  input  [13:0] control,
  input  [1:0] lbu_choose,
  input  [4:0] W_num,
  input  [4:0] rs,
  input  clk,
  input  [4:0] rt,
  input  [31:0] R2,
  input  [31:0] R,
  input  [31:0] data,
  input  clear,
  input  [4:0] rd,
  output syscall,
  output mem_reg,
  output [31:0] pc,
  output jal,
  output reg_write,
  output reg_dst,
  output [31:0] IR_2,
  output lbu,
  output alu_count,
  output jump_count,
  output branch_count,
  output mem_count,
  output other_count,
  output [31:0] R_2,
  output [31:0] data_2,
  output [31:0] R2_2,
  output [4:0] rt_2,
  output [4:0] rd_2,
  output [4:0] rs_2,
  output [4:0] W_num_2,
  output [1:0] lbu_choose_2
);

  wire [12:10] register_3_q;

  Register #(.width(32)) register_1 (.D(pc_4), .en(1'b1), .Q(pc), .clk(clk));  // open: clr
  Register #(.width(32)) register_2 (.D(IR), .en(1'b1), .Q(IR_2), .clk(clk));  // open: clr
  Register #(.width(14)) register_3 (
    .D(control), .en(1'b1),
    .Q({other_count, register_3_q, mem_count, branch_count, jump_count, alu_count, lbu, reg_dst, reg_write, jal, mem_reg, syscall}),
    .clk(clk));  // open: clr
  Register #(.width(32)) register_4 (.D(R), .en(1'b1), .Q(R_2), .clk(clk));  // open: clr
  Register #(.width(32)) register_5 (.D(data), .en(1'b1), .Q(data_2), .clk(clk));  // open: clr
  Register #(.width(32)) register_6 (.D(R2), .en(1'b1), .Q(R2_2), .clk(clk));  // open: clr
  Register #(.width(5)) register_7 (.D(rt), .en(1'b1), .Q(rt_2), .clk(clk));  // open: clr
  Register #(.width(5)) register_8 (.D(rd), .en(1'b1), .Q(rd_2), .clk(clk));  // open: clr
  Register #(.width(5)) register_9 (.D(rs), .en(1'b1), .Q(rs_2), .clk(clk));  // open: clr
  Register #(.width(5)) register_10 (.D(W_num), .en(1'b1), .Q(W_num_2), .clk(clk));  // open: clr
  Register #(.width(2)) register_11 (.D(lbu_choose), .en(1'b1), .Q(lbu_choose_2), .clk(clk));  // open: clr

  // Notes on the sheet:
  //   input
endmodule

// 重定向
module \data重定向机制  (
  input  [4:0] rs_EX,
  input  [4:0] W__Mem,
  input  mem_write_EX,
  input  reg_dst_EX,
  input  [4:0] rt_EX,
  input  [4:0] W__Wb,
  input  mem_write_Mem,
  input  [4:0] rt_Mem,
  input  [4:0] rs_ID,
  input  [4:0] rt_ID,
  input  reg_dst_ID,
  input  s_src,
  input  bne,
  input  beq,
  output Mem__EX_X,
  output Mem__EX_Y,
  output Wb__EX_X,
  output Wb__EX_Y,
  output Wb__Mem,
  output Wb__EX_R2,
  output Wb__ID_R1,
  output Wb__ID_R2
);

  wire and_1_out, and_2_out, and_7_out, comparator_1_eq, comparator_2_eq, comparator_3_eq, comparator_4_eq,
       comparator_5_eq, comparator_6_eq, comparator_7_eq, comparator_8_eq, or_1_out, or_2_out, or_3_out,
       or_4_out, or_5_out, or_6_out, or_7_out, or_9_out, or_10_out;

  or or_1 (or_1_out, rs_EX[0], rs_EX[1], rs_EX[2], rs_EX[3], rs_EX[4]);
  or or_2 (or_2_out, rs_EX[0], rs_EX[1], rs_EX[2], rs_EX[3], rs_EX[4]);
  or or_3 (or_3_out, rs_ID[0], rs_ID[1], rs_ID[2], rs_ID[3], rs_ID[4]);
  or or_4 (or_4_out, rt_EX[0], rt_EX[1], rt_EX[2], rt_EX[3], rt_EX[4]);
  or or_5 (or_5_out, rt_EX[0], rt_EX[1], rt_EX[2], rt_EX[3], rt_EX[4]);
  or or_6 (or_6_out, rt_ID[0], rt_ID[1], rt_ID[2], rt_ID[3], rt_ID[4]);
  Comparator #(.width(5)) comparator_1 (.a(rs_EX), .b(W__Mem), .eq(comparator_1_eq));  // open: gt, lt
  Comparator #(.width(5)) comparator_2 (.a(rt_EX), .b(W__Mem), .eq(comparator_2_eq));  // open: gt, lt
  or or_7 (or_7_out, reg_dst_EX, bne, beq);
  Comparator #(.width(5)) comparator_3 (.a(rs_EX), .b(W__Wb), .eq(comparator_3_eq));  // open: gt, lt
  Comparator #(.width(5)) comparator_4 (.a(rt_Mem), .b(W__Wb), .eq(comparator_4_eq));  // open: gt, lt
  Comparator #(.width(5)) comparator_5 (.a(rs_ID), .b(W__Wb), .eq(comparator_5_eq));  // open: gt, lt
  Comparator #(.width(5)) comparator_6 (.a(rt_ID), .b(W__Wb), .eq(comparator_6_eq));  // open: gt, lt
  and and_1 (and_1_out, comparator_1_eq, or_1_out);
  and and_2 (and_2_out, comparator_2_eq, or_7_out, or_4_out);
  and and_3 (Wb__EX_X, comparator_3_eq, or_2_out);
  and and_4 (Wb__Mem, comparator_4_eq, mem_write_Mem, or_5_out);
  and and_5 (Wb__ID_R1, comparator_5_eq, or_3_out);
  and and_6 (Wb__ID_R2, comparator_6_eq, reg_dst_ID, or_6_out);
  and and_7 (and_7_out, s_src, and_2_out);
  and and_8 (Mem__EX_Y, and_2_out, ~s_src);  // AND_Gate
  or or_8 (Mem__EX_X, and_1_out, and_7_out);
  or or_9 (or_9_out, rt_EX[0], rt_EX[1], rt_EX[2], rt_EX[3], rt_EX[4]);
  Comparator #(.width(5)) comparator_7 (.a(rt_EX), .b(W__Wb), .eq(comparator_7_eq));  // open: gt, lt
  Comparator #(.width(5)) comparator_8 (.a(rt_EX), .b(W__Wb), .eq(comparator_8_eq));  // open: gt, lt
  or or_10 (or_10_out, rt_EX[0], rt_EX[1], rt_EX[2], rt_EX[3], rt_EX[4]);
  and and_9 (Wb__EX_Y, comparator_7_eq, reg_dst_EX, or_9_out);
  and and_10 (Wb__EX_R2, comparator_8_eq, mem_write_EX, or_10_out);

  // Notes on the sheet:
  //   input
endmodule

// load_use
module \load_use检测  (
  input  [4:0] rs_ID,
  input  mem_read,
  input  [4:0] rt_ID,
  input  [4:0] rt_EX,
  output load_use
);

  wire comparator_1_eq, comparator_2_eq, or_1_out;

  Comparator #(.width(5)) comparator_1 (.a(rs_ID), .b(rt_EX), .eq(comparator_1_eq));  // open: gt, lt
  Comparator #(.width(5)) comparator_2 (.a(rt_ID), .b(rt_EX), .eq(comparator_2_eq));  // open: gt, lt
  or or_1 (or_1_out, comparator_1_eq, comparator_2_eq);
  and and_1 (load_use, or_1_out, mem_read);

  // Notes on the sheet:
  //   input
endmodule
