// Logisim project CS1409_U201414816_曾圳_cpu.circ as structural Verilog: 5 circuits, main circuit main
module main (
);

  wire _1_out, _2_out, _3_out, a_c, alu_src, and_1_out, and_2_out, and_3_out, and_4_out, and_5_out,
       and_7_out, b_c, bltz_ctr, branch_eq, branch_ne, clk, clock_1_out, comparator_1_eq, cp0_write, equal,
       eret, halt, imm, interrupt, interrupt_1__1, interrupt_1__2, interrupt_1__3, j_c, jal, jr, jump, lbu,
       m_c, mem_read, mem_reg, mem_write, mfc0, not_1_out, not_2_out, o_c, or_1_out, reg_dst, reg_write,
       sll_ra_rl, syscall;
  wire [1:0] number;
  wire [3:0] alu, register_2_q, register_2_q_2, register_2_q_3, register_2_q_4, register_2_q_5,
       register_2_q_6, register_2_q_7;
  wire [4:0] multiplexer_1_out, rd, rs, rt, W_num;
  wire [5:0] func, op;
  wire [8:0] demultiplexer_1_out0, demultiplexer_1_out1;
  wire [9:0] shifter_3_out;
  wire [10:6] multiplexer_7_out;
  wire [11:0] counter_2_alu_num, counter_2_branch_num, counter_2_clk_num, counter_2_jump_num,
       counter_2_mem_num, counter_2_other_num;
  wire [31:0] adder_2_out, bit_extender_1_out, bit_extender_2_out, bit_extender_3_out, bit_extender_4_out,
       bit_extender_5_out, cause, counter_1_q, epc, \mips寄存器组_1_a0 , \mips寄存器组_1_ra , \mips寄存器组_1_s0 ,
       \mips寄存器组_1_s1 , \mips寄存器组_1_s2 , \mips寄存器组_1_s3 , \mips寄存器组_1_v0 , multiplexer_4_out,
       multiplexer_5_out, multiplexer_8_out, multiplexer_9_out, multiplexer_10_out, multiplexer_11_out,
       multiplexer_12_out, multiplexer_14_out, multiplexer_15_out, multiplexer_16_out, multiplexer_17_out,
       multiplexer_18_out, multiplexer_19_out, pc, pc_4, pc_cu, pc_final, R, R1, R2, R_cp0, ram_1_data,
       rom_1_data, rom_2_data, shifter_1_out, shifter_2_out, status, vaddr;
  wire [31:28] register_2_q_8;

  Clock clock_1 (.out(clock_1_out));
  Register #(.width(32)) register_1 (.D(pc_final), .en(1'b1), .Q(pc_cu), .clk(clk), .clr(1'b0));
  Multiplexer #(.width(5), .enable("false")) multiplexer_1 (.in0(rt), .in1(rd), .out(multiplexer_1_out), .sel(reg_dst));
  Multiplexer #(.width(5), .enable("false")) multiplexer_2 (
    .in0(multiplexer_1_out), .in1({5{1'b1}}), .out(W_num), .sel(jal));
  Multiplexer #(.enable("false")) multiplexer_3 (.in0(clock_1_out), .in1(1'b1), .out(clk), .sel(halt));
  Demultiplexer #(.width(9)) demultiplexer_1 (
    .out0(demultiplexer_1_out0), .out1(demultiplexer_1_out1), .in(pc_cu[10:2]), .sel(pc_cu[11]), .en(1'b1));
  Multiplexer #(.width(32), .enable("false")) multiplexer_4 (.in0(pc), .in1(R1), .out(multiplexer_4_out), .sel(jr));
  Adder #(.width(32)) adder_1 (.a(pc_cu), .b(32'h4), .out(pc_4), .cin(1'b0));  // open: cout
  Multiplexer #(.width(32), .enable("false")) multiplexer_5 (
    .in0(multiplexer_4_out), .in1(epc), .out(multiplexer_5_out), .sel(eret));
  Counter #(.width(32), .max('hffffffff)) counter_1 (
    .load(1'b0), .D({32{1'b0}}), .count(1'b1), .Q(counter_1_q), .clk(clk), .clr(1'b0));  // open: carry
  ROM #(.addrWidth(9), .dataWidth(32)) rom_1 (.addr(demultiplexer_1_out0), .data(rom_1_data), .sel(1'b1));
  ROM #(.addrWidth(9), .dataWidth(32)) rom_2 (.addr(demultiplexer_1_out1), .data(rom_2_data), .sel(1'b1));
  Multiplexer #(.width(32), .enable("false")) multiplexer_6 (
    .in0(multiplexer_5_out), .in1(32'h800), .out(pc_final), .sel(interrupt));
  // Probe on counter_1_q
  // Probe on pc_final
  Multiplexer #(.width(32)) multiplexer_7 (
    .in0(rom_1_data), .in1(rom_2_data), .out({op, rs, rt, rd, multiplexer_7_out, func}), .sel(pc_cu[11]),
    .en(1'b1));
  Button _1 (.out(_1_out));
  Button _2 (.out(_2_out));
  Button _3 (.out(_3_out));
  assign bit_extender_1_out = {{30{1'b0}}, number};  // Bit_Extender bit_extender_1
  // Probe on number
  // Probe on rt
  assign bit_extender_2_out = {{16{rd[4]}}, {rd, multiplexer_7_out, func}};  // Bit_Extender bit_extender_2
  assign bit_extender_3_out = {{16{1'b0}}, {rd, multiplexer_7_out, func}};  // Bit_Extender bit_extender_3
  assign bit_extender_4_out = {{27{1'b0}}, multiplexer_7_out};  // Bit_Extender bit_extender_4
  Shifter #(.width(32)) shifter_1 (
    .in({op, rs, rt, rd, multiplexer_7_out, func}), .\dist (5'b00010), .out(shifter_1_out));
  Multiplexer #(.width(32), .enable("false")) multiplexer_8 (
    .in0(bit_extender_2_out), .in1(bit_extender_3_out), .out(multiplexer_8_out), .sel(imm));
  interrupt interrupt_1 (
    .status(status), .clk(clk), .number(number), .b_1(_1_out), .b_2(_2_out), .b_3(_3_out), .eret(eret),
    .cause(cause), .interrupt(interrupt), ._1(interrupt_1__1), ._2(interrupt_1__2), ._3(interrupt_1__3));
  Multiplexer #(.width(32)) multiplexer_9 (
    .in0(R2), .in1(bit_extender_1_out), .out(multiplexer_9_out), .sel(interrupt), .en(1'b1));
  // Probe on pc_cu
  Shifter #(.width(32)) shifter_2 (.in(multiplexer_8_out), .\dist (5'b00010), .out(shifter_2_out));
  // Probe on \mips寄存器组_1_s0 
  and and_1 (and_1_out, reg_write, ~interrupt);  // AND_Gate
  LED _1_2 (.in(interrupt_1__1));
  LED _2_2 (.in(interrupt_1__2));
  LED _3_2 (.in(interrupt_1__3));
  cp0 cp0_1 (
    .clk(clk), .Din(multiplexer_9_out), .epc(epc), .vaddr(vaddr), .status(status), .cause(cause), .W_num(rd),
    .WE(cp0_write), .R(R_cp0), .R_num(rd), .PC(pc_cu), .interrupt(interrupt));
  Adder #(.width(32)) adder_2 (.a(pc_4), .b(shifter_2_out), .out(adder_2_out), .cin(1'b0));  // open: cout
  not not_1 (not_1_out, equal);
  // Probe on \mips寄存器组_1_s1 
  // Probe on \mips寄存器组_1_s3 
  // Probe on epc
  // Probe on cause
  or or_1 (or_1_out, and_2_out, and_3_out, and_4_out);
  and and_2 (and_2_out, not_1_out, branch_ne);
  and and_3 (and_3_out, bltz_ctr, R[0]);
  // Probe on \mips寄存器组_1_ra 
  // Probe on \mips寄存器组_1_s2 
  \MIPS寄存器组  \mips寄存器组_1  (
    .W_num(W_num), .Din(multiplexer_16_out), .WE(and_1_out), .R2_num(rt), .R1_num(rs), .s0(\mips寄存器组_1_s0 ),
    .s1(\mips寄存器组_1_s1 ), .s2(\mips寄存器组_1_s2 ), .ra(\mips寄存器组_1_ra ), .R1(R1), .R2(R2), .clk(clk),
    .v0(\mips寄存器组_1_v0 ), .s3(\mips寄存器组_1_s3 ), .a0(\mips寄存器组_1_a0 ));  // open: s4
  Multiplexer #(.width(32), .enable("false")) multiplexer_10 (
    .in0(R2), .in1(multiplexer_8_out), .out(multiplexer_10_out), .sel(alu_src));
  not not_2 (not_2_out, halt);
  // Probe on vaddr
  Multiplexer #(.width(32), .enable("false")) multiplexer_11 (
    .in0(pc_4), .in1(adder_2_out), .out(multiplexer_11_out), .sel(or_1_out));
  and and_4 (and_4_out, branch_eq, equal);
  Multiplexer #(.width(32), .enable("false")) multiplexer_12 (
    .in0(multiplexer_10_out), .in1(bit_extender_4_out), .out(multiplexer_12_out), .sel(sll_ra_rl));
  and and_5 (and_5_out, syscall, not_2_out);
  Multiplexer #(.width(32), .enable("false")) multiplexer_13 (
    .in0(multiplexer_11_out), .in1({pc_4[31:28], shifter_1_out[27:0]}), .out(pc), .sel(jump));
  Comparator #(.width(32)) comparator_1 (.a(32'ha), .b(\mips寄存器组_1_v0 ), .eq(comparator_1_eq));  // open: gt, lt
  Multiplexer #(.width(32), .enable("false")) multiplexer_14 (
    .in0(R1), .in1(R2), .out(multiplexer_14_out), .sel(sll_ra_rl));
  Hex_Digit_Display hex_digit_display_1 (.value(register_2_q_8));  // open: dp
  Hex_Digit_Display hex_digit_display_2 (.value(register_2_q_7));  // open: dp
  Register #(.width(32)) register_2 (
    .D(\mips寄存器组_1_a0 ), .en(and_5_out),
    .Q({register_2_q_8, register_2_q_7, register_2_q_6, register_2_q_5, register_2_q_4, register_2_q_3, register_2_q_2, register_2_q}),
    .clk(clk), .clr(1'b0));
  and and_6 (halt, syscall, comparator_1_eq);
  Multiplexer #(.width(32), .enable("false")) multiplexer_15 (
    .in0(multiplexer_12_out), .in1({32{1'b0}}), .out(multiplexer_15_out), .sel(bltz_ctr));
  Hex_Digit_Display hex_digit_display_3 (.value(register_2_q_6));  // open: dp
  Hex_Digit_Display hex_digit_display_4 (.value(register_2_q_5));  // open: dp
  // Probe on counter_2_mem_num
  // Probe on counter_2_alu_num
  // Probe on counter_2_other_num
  counter counter_2 (
    .mem_count(m_c), .alu_count(a_c), .jump_count(j_c), .branch_count(b_c), .mem_num(counter_2_mem_num),
    .alu_num(counter_2_alu_num), .jump_num(counter_2_jump_num), .branch_num(counter_2_branch_num),
    .clk_num(counter_2_clk_num), .clk_count(clk), .other_num(counter_2_other_num), .other_count(o_c));
  // Probe on counter_2_jump_num
  // Probe on counter_2_branch_num
  // Probe on counter_2_clk_num
  Hex_Digit_Display hex_digit_display_5 (.value(register_2_q_4));  // open: dp
  Hex_Digit_Display hex_digit_display_6 (.value(register_2_q_3));  // open: dp
  ALU alu_2 (
    .AluOP(alu), .X(multiplexer_14_out), .Equal(equal), .Result(R), .Y(multiplexer_15_out));  // open: Signed_Overflow, Result_2, UnSigned_Overflow
  Hex_Digit_Display hex_digit_display_7 (.value(register_2_q_2));  // open: dp
  Hex_Digit_Display hex_digit_display_8 (.value(register_2_q));  // open: dp
  Multiplexer #(.width(32), .enable("false")) multiplexer_16 (
    .in0(multiplexer_17_out), .in1(R_cp0), .out(multiplexer_16_out), .sel(mfc0));
  Shifter #(.width(10), .shift("ar")) shifter_3 (.in(R[9:0]), .\dist (4'b0010), .out(shifter_3_out));
  Multiplexer #(.width(32), .enable("false")) multiplexer_17 (
    .in0(multiplexer_18_out), .in1(bit_extender_5_out), .out(multiplexer_17_out), .sel(lbu));
  controller controller_1 (
    .op(op), .func(func), .alu_op(alu), .reg_dst(reg_dst), .branch_ne(branch_ne), .jump(jump),
    .reg_write(reg_write), .mem_read(mem_read), .mem_write(mem_write), .alu_src(alu_src), .mem_reg(mem_reg),
    .syacall(syscall), .branch_eq(branch_eq), .jr(jr), .jal(jal), .sll_ra(sll_ra_rl), .andi_ori_sltiu(imm),
    .alu_count(a_c), .jump_count(j_c), .branch_count(b_c), .mem_count(m_c), .other_count(o_c), .lbu(lbu),
    .bltz(rt), .bltz_ctr(bltz_ctr), .eret(eret), .interrupt(rs), .cp0_write(cp0_write), .mfc0(mfc0));
  and and_7 (and_7_out, mem_write, ~interrupt);  // AND_Gate
  RAM #(.addrWidth(10), .dataWidth(32), .bus("separate")) ram_1 (
    .addr(shifter_3_out), .din(R2), .data(ram_1_data), .str(and_7_out), .sel(1'b1), .clk(clk), .ld(mem_read),
    .clr(1'b0));
  Multiplexer #(.width(32), .enable("false")) multiplexer_18 (
    .in0(multiplexer_19_out), .in1(pc_4), .out(multiplexer_18_out), .sel(jal));
  assign bit_extender_5_out = {{24{1'b0}}, multiplexer_18_out[7:0]};  // Bit_Extender bit_extender_5
  Multiplexer #(.width(32), .enable("false")) multiplexer_19 (
    .in0(ram_1_data), .in1(R), .out(multiplexer_19_out), .sel(mem_reg));

  // Other names for the same wires on the sheet: is = interrupt

  // Notes on the sheet:
  //   contents of rom_1 (hex, n*v repeats v):
  //   20110001 8000c05 20110001 20120002 20130003 8000c09 20110001 20120002 20130003 8000c0d 20110001
  //   20120002 20130003 8000c11 20110001 20120002 20130003 c000cb8 20100001 20110001 118fc0 112020
  //   20020022 c 118882 12200001 8000c15 112020 20020022 c 20110001 118880 112020 20020022 c 12200001
  //   8000c1f 20110001 118fc0 112020 20020022 c 1188c3 112020 20020022 c 118903 112020 20020022 c 118903
  //   112020 20020022 c 118903 112020 20020022 c 118903 112020 20020022 c 118903 112020 20020022 c 118903
  //   112020 20020022 c 118903 112020 20020022 c 20100001 109fc0 139fc3 8021 2012000c 24160003 26100001
  //   3210000f 20080008 20090001 139900 2709825 132020 20020022 c 1094022 1500fff9 22100001 2018000f
  //   2188024 108700 20080008 20090001 139902 2709825 132021 20020022 c 1094022 1500fff9 108702 2c9b022
  //   12c00001 8000c50 4020 1084027 84400 3508ffff 82021 20020022 c 2010ffff 20110000 ae300000 22100001
  //   22310004 ae300000 22100001 22310004 ae300000 22100001 22310004 ae300000 22100001 22310004 ae300000
  //   22100001 22310004 ae300000 22100001 22310004 ae300000 22100001 22310004 ae300000 22100001 22310004
  //   ae300000 22100001 22310004 ae300000 22100001 22310004 ae300000 22100001 22310004 ae300000 22100001
  //   22310004 ae300000 22100001 22310004 ae300000 22100001 22310004 ae300000 22100001 22310004 ae300000
  //   22100001 22310004 22100001 8020 2011003c 8e130000 8e340000 274402a 11000002 ae330000 ae140000
  //   2231fffc 1611fff8 102020 20020022 c 22100004 2011003c 1611fff2 2002000a c 20100000 22100001 102020
  //   20020022 c 22100002 102020 20020022 c 22100003 102020 20020022 c 22100004 102020 20020022 c 22100005
  //   102020 20020022 c 22100006 102020 20020022 c 22100007 102020 20020022 c 22100008 102020 20020022
  //   20020022 c 3e00008
  //   contents of rom_2 (hex, n*v repeats v):
  //   401a6000 375a0001 409a6000 23bd0080 afb00000 23bd0004 40106000 108043 108040 afb00000 23bd0004
  //   afb10000 23bd0004 afa20000 23bd0004 afa40000 23bd0004 afba0000 23bd0004 40107000 afb00000 23bd0004
  //   afbe0000 23bd0004 40116800 20100001 12300004 20100002 12300006 20100003 12300008 20110003 40916000
  //   20110001 12300008 20110007 40916000 20110002 12300004 2011000f 40916000 20110003 12300000 401a6000
  //   1ad043 1ad040 409a6000 40116800 20100001 12300006 20100002 12300011 20100003 1230001c 20100000
  //   12000026 20110000 20020022 22040000 c 108100 1630fffc 20100001 108700 22040000 c 108103 1630fffc
  //   12300019 20110000 20020022 22040000 c 108100 1630fffc 20100002 108700 22040000 c 108103 1630fffc
  //   1230000c 20110000 20020022 22040000 c 108100 1630fffc 20100003 108700 22040000 c 108103 1630fffc
  //   20040000 c 401a6000 375a0001 409a6000 23bdfffc 8fbe0000 23bdfffc 8fb00000 40907000 23bdfffc 8fba0000
  //   23bdfffc 8fa40000 23bdfffc 8fa20000 23bdfffc 8fb10000 23bdfffc 8fb00000 36100001 40906000 23bdfffc
  //   8fb00000 23bdff80 401a6000 1ad043 1ad040 409a6000 42000018
endmodule

// 控制单元
module controller (
  input  [4:0] bltz,
  input  [4:0] interrupt,
  input  [5:0] op,
  input  [5:0] func,
  output branch_eq,
  output branch_ne,
  output jump,
  output lbu,
  output mem_read,
  output mem_write,
  output syacall,
  output jr,
  output jal,
  output sll_ra,
  output andi_ori_sltiu,
  output jump_count,
  output branch_count,
  output mem_count,
  output other_count,
  output bltz_ctr,
  output eret,
  output cp0_write,
  output mfc0,
  output reg_dst,
  output reg_write,
  output alu_src,
  output mem_reg,
  output alu_count,
  output [3:0] alu_op
);

  wire add, addi, addiu, addu, alu_count_out, alu_src_out, \and , and_14_out, andi, eret_2_out, eret_3_out,
       j, lw, mem_reg_3_out, mem_reg_out, mfc0_3_out, mfc0_out, mtc0, \nor , op_t, \or , or_1_out, or_2_out,
       or_4_out, or_5_out, ori, reg_dst_out, reg_write_2_out, reg_write_3_out, reg_write_out, sll, slt, slti,
       sltiu, sltu, sra, srl, sub, \xor ;
  wire [3:0] and_1_out, and_2_out, and_3_out, and_4_out, and_5_out, and_6_out, and_7_out, and_9_out,
       and_10_out, and_11_out, and_12_out, and_13_out, bit_extender_1_out, bit_extender_2_out,
       bit_extender_3_out, bit_extender_4_out, bit_extender_5_out, bit_extender_6_out, bit_extender_7_out,
       bit_extender_8_out, bit_extender_9_out, bit_extender_10_out, bit_extender_11_out, bit_extender_12_out,
       or_3_out, or_7_out;
  wire [4:0] not_3_out, not_4_out;
  wire [5:0] not_1_out, not_2_out;

  assign not_1_out = ~op;  // NOT_Gate not_1, 6 bits wide
  assign not_2_out = ~func;  // NOT_Gate not_2, 6 bits wide
  and u_op (op_t, not_1_out[0], not_1_out[1], not_1_out[2], not_1_out[3], not_1_out[4], not_1_out[5]);
  and u_add (add, not_2_out[4], not_2_out[3], not_2_out[2], not_2_out[1], not_2_out[0], func[5], op_t);
  or u_reg_dst (reg_dst_out, add, addu, \and , sll, sra, srl, sub, \or , \nor , slt, sltu);
  or reg_dst_2 (reg_dst, reg_dst_out, \xor );
  or or_1 (or_1_out, lbu, add, addiu, addi, mem_write, lw, addu);
  assign bit_extender_1_out = {{3{or_1_out}}, or_1_out};  // Bit_Extender bit_extender_1
  assign bit_extender_2_out = {{3{\xor }}, \xor };  // Bit_Extender bit_extender_2
  assign bit_extender_3_out = {{3{or_2_out}}, or_2_out};  // Bit_Extender bit_extender_3
  or or_2 (or_2_out, \and , andi);
  assign bit_extender_4_out = {{3{sll}}, sll};  // Bit_Extender bit_extender_4
  and u_lw (lw, op[0], op[1], op[5], not_1_out[2], not_1_out[3], not_1_out[4]);
  and u_addi (addi, op[3], not_1_out[0], not_1_out[1], not_1_out[2], not_1_out[4], not_1_out[5]);
  assign and_1_out = bit_extender_1_out & 4'b0101;  // AND_Gate and_1, 4 bits wide
  assign and_2_out = bit_extender_2_out & 4'b1001;  // AND_Gate and_2, 4 bits wide
  assign and_3_out = bit_extender_3_out & 4'b0111;  // AND_Gate and_3, 4 bits wide
  assign and_4_out = bit_extender_4_out & 4'b0000;  // AND_Gate and_4, 4 bits wide
  and sw (mem_write, op[0], op[1], op[3], op[5], not_1_out[2], not_1_out[4]);
  and u_addiu (addiu, op[0], op[3], not_1_out[1], not_1_out[2], not_1_out[4], not_1_out[5]);
  or u_jump (jump, jr, jal, j);
  assign bit_extender_5_out = {{3{sra}}, sra};  // Bit_Extender bit_extender_5
  assign bit_extender_6_out = {{3{srl}}, srl};  // Bit_Extender bit_extender_6
  assign bit_extender_7_out = {{3{\nor }}, \nor };  // Bit_Extender bit_extender_7
  and beq (branch_eq, op[2], not_1_out[0], not_1_out[1], not_1_out[3], not_1_out[4], not_1_out[5]);
  and u_addu (addu, func[0], func[5], not_2_out[1], not_2_out[2], not_2_out[3], not_2_out[4], op_t);
  assign and_5_out = bit_extender_5_out & 4'b0001;  // AND_Gate and_5, 4 bits wide
  assign and_6_out = bit_extender_6_out & 4'b0010;  // AND_Gate and_6, 4 bits wide
  assign and_7_out = bit_extender_7_out & 4'b1010;  // AND_Gate and_7, 4 bits wide
  and and_8 (\and , func[2], func[5], not_2_out[0], not_2_out[1], not_2_out[3], not_2_out[4], op_t);
  or u_reg_write (reg_write_out, add, addu, \and , sll, sra, srl, sub, \or , \nor , slt, sltu);
  or reg_write_2 (reg_write_2_out, reg_write_out, \xor , lbu, sltiu, reg_write_3_out);
  and bne (branch_ne, op[0], op[2], not_1_out[1], not_1_out[3], not_1_out[4], not_1_out[5]);
  and u_andi (andi, op[2], op[3], not_1_out[0], not_1_out[1], not_1_out[4], not_1_out[5]);
  or reg_write_3 (reg_write_3_out, ori, andi, addi, jal, addiu, slti, lw);
  or reg_write_4 (reg_write, reg_write_2_out, mfc0);
  assign or_3_out = and_1_out | and_5_out | and_2_out | and_6_out | and_3_out | and_7_out | and_4_out;  // OR_Gate or_3, 4 bits wide
  and u_slti (slti, op[1], op[3], not_1_out[0], not_1_out[2], not_1_out[4], not_1_out[5]);
  and u_sll (sll, not_2_out[0], not_2_out[1], not_2_out[2], not_2_out[3], not_2_out[4], not_2_out[5], op_t);
  or u_mem_read (mem_read, lw, lbu);
  assign bit_extender_8_out = {{3{or_4_out}}, or_4_out};  // Bit_Extender bit_extender_8
  or or_4 (or_4_out, sltu, sltiu);
  or or_5 (or_5_out, slt, bltz_ctr, slti);
  and u_j (j, op[1], not_1_out[0], not_1_out[2], not_1_out[3], not_1_out[4], not_1_out[5]);
  and u_sra (sra, func[0], func[1], not_2_out[2], not_2_out[3], not_2_out[4], not_2_out[5], op_t);
  assign and_9_out = bit_extender_8_out & 4'b1100;  // AND_Gate and_9, 4 bits wide
  assign bit_extender_9_out = {{3{or_5_out}}, or_5_out};  // Bit_Extender bit_extender_9
  assign and_10_out = bit_extender_9_out & 4'b1011;  // AND_Gate and_10, 4 bits wide
  and u_jal (jal, op[0], op[1], not_1_out[2], not_1_out[3], not_1_out[4], not_1_out[5]);
  and u_srl (srl, func[1], not_2_out[0], not_2_out[2], not_2_out[3], not_2_out[4], not_2_out[5], op_t);
  assign bit_extender_10_out = {{3{sub}}, sub};  // Bit_Extender bit_extender_10
  assign bit_extender_11_out = {{3{ori}}, ori};  // Bit_Extender bit_extender_11
  assign bit_extender_12_out = {{3{\or }}, \or };  // Bit_Extender bit_extender_12
  and u_sltiu (sltiu, op[0], op[1], op[3], not_1_out[2], not_1_out[4], not_1_out[5]);
  and u_sub (sub, func[1], func[5], not_2_out[0], not_2_out[2], not_2_out[3], not_2_out[4], op_t);
  or u_alu_src (alu_src_out, ori, andi, addi, lw, addiu, slti, mem_write);
  or alu_src_2 (alu_src, alu_src_out, lbu, sltiu);
  assign and_11_out = bit_extender_10_out & 4'b0110;  // AND_Gate and_11, 4 bits wide
  assign and_12_out = bit_extender_11_out & 4'b1000;  // AND_Gate and_12, 4 bits wide
  assign and_13_out = bit_extender_12_out & 4'b1000;  // AND_Gate and_13, 4 bits wide
  and or_6 (\or , func[0], func[2], func[5], not_2_out[1], not_2_out[3], not_2_out[4], op_t);
  or u_mem_reg (mem_reg_out, add, addu, \and , sll, sra, srl, sub, \or , \nor , slt, sltu);
  and u_lbu (lbu, op[2], op[5], not_1_out[0], not_1_out[1], not_1_out[3], not_1_out[4]);
  and u_ori (ori, op[0], op[2], op[3], not_1_out[1], not_1_out[4], not_1_out[5]);
  or mem_reg_2 (mem_reg, mem_reg_out, \xor , sltiu, mem_reg_3_out);
  assign or_7_out = and_9_out | and_11_out | and_12_out | and_13_out | and_10_out;  // OR_Gate or_7, 4 bits wide
  and u_bltz (bltz_ctr, op[0], not_1_out[1], not_1_out[2], not_1_out[3], not_1_out[4], not_1_out[5], and_14_out);
  and u_nor (\nor , func[0], func[1], func[2], func[5], not_2_out[3], not_2_out[4], op_t);
  or mem_reg_3 (mem_reg_3_out, ori, andi, addi, addiu, slti);
  assign alu_op = or_3_out | or_7_out;  // OR_Gate or_8, 4 bits wide
  and and_14 (and_14_out, not_3_out[0], not_3_out[1], not_3_out[2], not_3_out[3], not_3_out[4]);
  and u_slt (slt, func[1], func[3], func[5], not_2_out[0], not_2_out[2], not_2_out[4], op_t);
  assign not_3_out = ~bltz;  // NOT_Gate not_3, 5 bits wide
  and u_sltu (sltu, func[0], func[1], func[3], func[5], not_2_out[2], not_2_out[4], op_t);
  and u_jr (jr, func[3], not_2_out[0], not_2_out[1], not_2_out[2], not_2_out[4], not_2_out[5], op_t);
  and u_eret (eret, eret_2_out, eret_3_out);
  and eret_2 (eret_2_out, op[4], not_1_out[0], not_1_out[1], not_1_out[2], not_1_out[3], not_1_out[5]);
  and syscall (syacall, func[2], func[3], not_2_out[0], not_2_out[1], not_2_out[4], not_2_out[5], op_t);
  or u_sll_ra (sll_ra, sll, srl, sra);
  and eret_3 (eret_3_out, func[3], func[4], not_2_out[0], not_2_out[1], not_2_out[2], not_2_out[5]);
  and u_xor (\xor , op_t, func[1], func[2], func[5], not_2_out[0], not_2_out[4], op_t);
  or u_andi_ori_sltiu (andi_ori_sltiu, andi, sltiu, ori);
  or u_alu_count (alu_count_out, add, \and , sll, sra, srl, sub, \or , \nor , ori, andi, addi, addiu, slti);
  and u_mfc0 (mfc0_out, op[4], not_1_out[0], not_1_out[1], not_1_out[2], not_1_out[3], not_1_out[5]);
  or alu_count_2 (alu_count, alu_count_out, \xor , sltiu);
  and mfc0_2 (mfc0, mfc0_out, mfc0_3_out);
  or u_jump_count (jump_count, jr, jal, j);
  and mfc0_3 (mfc0_3_out, not_4_out[4], not_4_out[3], not_4_out[2], not_4_out[1], not_4_out[0]);
  and u_mtc0 (mtc0, mfc0_out, not_4_out[4], not_4_out[3], not_4_out[1], not_4_out[0], interrupt[2]);
  or u_branch_count (branch_count, branch_eq, branch_ne);
  or u_mem_count (mem_count, lw, lbu, mem_write);
  or u_other_count (other_count, sltu, slt, bltz_ctr, syacall, addu, eret, mfc0, mtc0);
  assign not_4_out = ~interrupt;  // NOT_Gate not_4, 5 bits wide
  or mem_count_2 (cp0_write, eret, mtc0);

  // Other names for the same wires on the sheet: beq = branch_eq; bltz_t = bltz_ctr; bne = branch_ne; sw = mem_write;
  //   syscall = syacall
endmodule

module counter (
  input  mem_count,
  input  alu_count,
  input  jump_count,
  input  branch_count,
  input  clk_count,
  input  other_count,
  output [11:0] mem_num,
  output [11:0] alu_num,
  output [11:0] jump_num,
  output [11:0] branch_num,
  output [11:0] clk_num,
  output [11:0] other_num
);

  wire [11:0] adder_1_out, adder_2_out, adder_3_out, adder_4_out, adder_5_out, adder_6_out;

  Register #(.width(12)) register_1 (.D(adder_1_out), .en(mem_count), .Q(mem_num), .clk(clk_count), .clr(1'b0));
  Register #(.width(12)) register_2 (.D(adder_2_out), .en(alu_count), .Q(alu_num), .clk(clk_count), .clr(1'b0));
  Register #(.width(12)) register_3 (.D(adder_3_out), .en(jump_count), .Q(jump_num), .clk(clk_count), .clr(1'b0));
  Register #(.width(12)) register_4 (.D(adder_4_out), .en(branch_count), .Q(branch_num), .clk(clk_count), .clr(1'b0));
  Register #(.width(12)) register_5 (.D(adder_5_out), .en(1'b1), .Q(clk_num), .clk(clk_count), .clr(1'b0));
  Register #(.width(12)) register_6 (.D(adder_6_out), .en(other_count), .Q(other_num), .clk(clk_count), .clr(1'b0));
  Adder #(.width(12)) adder_1 (.a(mem_num), .b(12'h1), .out(adder_1_out), .cin(1'b0));  // open: cout
  Adder #(.width(12)) adder_2 (.a(alu_num), .b(12'h1), .out(adder_2_out), .cin(1'b0));  // open: cout
  Adder #(.width(12)) adder_3 (.a(jump_num), .b(12'h1), .out(adder_3_out), .cin(1'b0));  // open: cout
  Adder #(.width(12)) adder_4 (.a(branch_num), .b(12'h1), .out(adder_4_out), .cin(1'b0));  // open: cout
  Adder #(.width(12)) adder_5 (.a(clk_num), .b(12'h1), .out(adder_5_out), .cin(1'b0));  // open: cout
  Adder #(.width(12)) adder_6 (.a(other_num), .b(12'h1), .out(adder_6_out), .cin(1'b0));  // open: cout
endmodule

module interrupt (
  input  clk,
  input  b_3,
  input  [31:0] status,
  input  [31:0] cause,
  input  b_1,
  input  eret,
  input  b_2,
  output [1:0] number,
  output _1,
  output _2,
  output _3,
  output interrupt
);

  wire and_2_out, and_3_out, and_4_out, c_1, c_2, c_3, IE_q, multiplexer_1_out, multiplexer_2_out,
       multiplexer_3_out, not_1_out, not_2_out, not_3_out, priority_encoder_1_gs, register_1_q, register_2_q,
       register_3_q, register_4_q, register_5_q, register_6_q, register_7_q, register_8_q, register_9_q,
       register_10_q;
  wire [1:0] priority_encoder_1_out;

  Register #(.width(1)) register_1 (.D(1'b1), .en(1'b1), .Q(register_1_q), .clk(b_1), .clr(c_1));
  Register #(.width(1)) register_2 (.D(1'b1), .en(1'b1), .Q(register_2_q), .clk(b_2), .clr(c_2));
  Register #(.width(1)) register_3 (.D(1'b1), .en(1'b1), .Q(register_3_q), .clk(b_3), .clr(c_3));
  not not_1 (not_1_out, register_4_q);
  Register #(.width(1)) register_4 (.D(status[1]), .en(1'b1), .Q(register_4_q), .clk(clk), .clr(1'b0));
  not not_2 (not_2_out, register_5_q);
  Register #(.width(1)) register_5 (.D(status[2]), .en(1'b1), .Q(register_5_q), .clk(clk), .clr(1'b0));
  not not_3 (not_3_out, register_6_q);
  Register #(.width(1)) register_6 (.D(status[3]), .en(1'b1), .Q(register_6_q), .clk(clk), .clr(1'b0));
  Register #(.width(1)) register_7 (.D(b_1), .en(1'b1), .Q(register_7_q), .clk(clk), .clr(1'b0));
  Multiplexer #(.enable("false")) multiplexer_1 (.in0(register_1_q), .in1(1'b0), .out(multiplexer_1_out), .sel(c_1));
  Multiplexer #(.enable("false")) multiplexer_2 (.in0(register_2_q), .in1(1'b0), .out(multiplexer_2_out), .sel(c_2));
  Multiplexer #(.enable("false")) multiplexer_3 (.in0(register_3_q), .in1(1'b0), .out(multiplexer_3_out), .sel(c_3));
  Register #(.width(1)) register_8 (.D(multiplexer_1_out), .en(1'b1), .Q(register_8_q), .clk(clk), .clr(1'b0));
  Register #(.width(1)) register_9 (.D(multiplexer_2_out), .en(1'b1), .Q(register_9_q), .clk(clk), .clr(1'b0));
  or or_1 (_2, register_9_q, register_2_q);
  or or_2 (_3, register_10_q, register_3_q);
  Register #(.width(1)) register_10 (.D(multiplexer_3_out), .en(1'b1), .Q(register_10_q), .clk(clk), .clr(1'b0));
  // AND_Gate and_1 has open pins: in0=register_7_q, in1=not_1_out, out=open
  or or_3 (_1, register_1_q, register_8_q);
  and and_2 (and_2_out, register_8_q, not_1_out);
  and and_3 (and_3_out, register_9_q, not_2_out);
  and and_4 (and_4_out, register_10_q, not_3_out);
  Register #(.width(1)) IE (.D(status[0]), .en(1'b1), .Q(IE_q), .clk(clk), .clr(1'b0));
  and and_5 (c_1, and_2_out, interrupt);
  and and_6 (c_2, and_3_out, interrupt);
  and and_7 (c_3, and_4_out, interrupt);
  Priority_Encoder #(.select(2)) priority_encoder_1 (
    .in0(1'b0), .in1(and_2_out), .in2(and_3_out), .in3(and_4_out), .out(priority_encoder_1_out),
    .gs(priority_encoder_1_gs), .en_in(1'b1));  // open: en_out
  and and_8 (interrupt, priority_encoder_1_gs, ~IE_q);  // AND_Gate
  // Probe on number
  Multiplexer #(.width(2)) multiplexer_4 (
    .in0(2'b00), .in1(priority_encoder_1_out), .out(number), .sel(priority_encoder_1_gs), .en(1'b1));

  // Other names for the same wires on the sheet: IE = status[0]; IP[2:0] = status[3:1]; change[1:0] = status[5:4]
endmodule

module cp0 (
  input  clk,
  input  WE,
  input  [4:0] W_num,
  input  [31:0] Din,
  input  [31:0] PC,
  input  [4:0] R_num,
  input  interrupt,
  output [31:0] epc,
  output [31:0] vaddr,
  output [31:0] status,
  output [31:0] cause,
  output [31:0] R
);

  wire demultiplexer_1_out8, demultiplexer_1_out12, demultiplexer_1_out13, demultiplexer_1_out14, or_1_out,
       or_2_out;
  wire [31:0] bit_extender_1_out, multiplexer_1_out, PC_buffer;

  Demultiplexer #(.select(5)) demultiplexer_1 (
    .out8(demultiplexer_1_out8), .out12(demultiplexer_1_out12), .out13(demultiplexer_1_out13),
    .out14(demultiplexer_1_out14), .in(WE), .sel(W_num), .en(1'b1));  // open: out0, out1, out2, out3, out4, out5, out6, out7, out9, out10, out11, out15, out16, out17, out18, out19, out20, out21, out22, out23, out24, out25, out26, out27, out28, out29, out30, out31
  or or_1 (or_1_out, demultiplexer_1_out13, interrupt);
  or or_2 (or_2_out, demultiplexer_1_out14, interrupt);
  Multiplexer #(.width(32)) multiplexer_1 (
    .in0(Din), .in1(PC_buffer), .out(multiplexer_1_out), .sel(interrupt), .en(1'b1));
  Register #(.width(32)) epc_buffer (.D(PC), .en(1'b1), .Q(PC_buffer), .clk(interrupt), .clr(1'b0));
  Register #(.width(32)) u_vaddr (.D(Din), .en(demultiplexer_1_out8), .Q(vaddr), .clk(clk), .clr(1'b0));
  Register #(.width(32)) u_status (.D(Din), .en(demultiplexer_1_out12), .Q(status), .clk(clk), .clr(1'b0));
  Register #(.width(32)) u_cause (.D(Din), .en(or_1_out), .Q(cause), .clk(clk), .clr(1'b0));
  Register #(.width(32)) u_epc (.D(multiplexer_1_out), .en(or_2_out), .Q(epc), .clk(clk), .clr(1'b0));
  assign bit_extender_1_out = {{31{1'b0}}, 1'b0};  // Bit_Extender bit_extender_1
  Multiplexer #(.select(5), .width(32)) multiplexer_2 (
    .in0(bit_extender_1_out), .in1(bit_extender_1_out), .in2(bit_extender_1_out), .in3(bit_extender_1_out),
    .in4(bit_extender_1_out), .in5(bit_extender_1_out), .in6(bit_extender_1_out), .in7(bit_extender_1_out),
    .in8(vaddr), .in9(bit_extender_1_out), .in10(bit_extender_1_out), .in11(bit_extender_1_out),
    .in12(status), .in13(cause), .in14(epc), .in15(bit_extender_1_out), .in16(bit_extender_1_out),
    .in17(bit_extender_1_out), .in18(bit_extender_1_out), .in19(bit_extender_1_out),
    .in20(bit_extender_1_out), .in21(bit_extender_1_out), .in22(bit_extender_1_out),
    .in23(bit_extender_1_out), .in24(bit_extender_1_out), .in25(bit_extender_1_out),
    .in26(bit_extender_1_out), .in27(bit_extender_1_out), .in28(bit_extender_1_out),
    .in29(bit_extender_1_out), .in30(bit_extender_1_out), .in31(bit_extender_1_out), .out(R), .sel(R_num),
    .en(1'b1));

  // Notes on the sheet:
  //   输入
  //   输出
endmodule
