// Logisim project CS1409_U201214816_曾圳_alu.circ as structural Verilog: 9 circuits, main circuit ALU
module ALU (
  input  [31:0] X,
  input  [31:0] Y,
  input  [3:0] AluOP,
  output Signed_Overflow,
  output UnSigned_Overflow,
  output Equal,
  output [31:0] Result,
  output [31:0] Result_2
);

  // Probe on X
  // Probe on X
  // Probe on Y
  // Probe on Y
  // Probe on AluOP
  \_32位运算器  \u_32位运算器_1  (
    .X(X), .Y(Y), .Result2(Result_2), .Result(Result), .OF(Signed_Overflow), .UOF(UnSigned_Overflow),
    .Equal(Equal), .ALU_OP(AluOP));
  // Probe on Result
  // Probe on Result
  // Probe on Result_2

  // Other names for the same wires on the sheet: OF = Signed_Overflow; Result2[31:0] = Result_2; S[3:0] = AluOP;
  //   UOF = UnSigned_Overflow

  // Notes on the sheet:
  //   不要改变此引脚区域内容，也不要改变ALU封装形式
  //   输入引脚
  //   请在下方利用上方输入输出引脚的隧道信号构建ALU电路，ctrl+d复制选择部件
  //   华中科技大学计算机学院 计算机组成原理，鸣谢加州大学伯克利CS61C课程
  //   输出引脚
  //   探测区域
endmodule

module \演示电路  (
  input  [31:0] X,
  input  [31:0] Y,
  input  [3:0] ALUOP,
  output Signed_Overflow,
  output Unsigned_overflow,
  output [31:0] Result,
  output [31:0] Result_2,
  output Equal
);

  // Probe on X
  // Probe on X
  ALU alu_1 (
    .AluOP(ALUOP), .X(X), .Equal(Equal), .Result(Result), .Signed_Overflow(Signed_Overflow), .Y(Y),
    .Result_2(Result_2), .UnSigned_Overflow(Unsigned_overflow));
  // Probe on ALUOP
  // Probe on Y
  // Probe on Y
  // Probe on Result
  // Probe on Result
  // Probe on Result_2

  // Notes on the sheet:
  //   ALu电路无需调整位置即可连接在该电路中，并且不能出现蓝色线缆和三态输出
endmodule

module \等差数列  (
  input  [31:0] \数列初始值 ,
  input  [31:0] \等差值 ,
  input  \时钟 ,
  output [31:0] Result
);

  // Probe on \数列初始值 
  // Probe on \数列初始值 
  // Probe on \等差值 
  // Probe on \等差值 
  // Probe on Result
  // Probe on Result

  // Other names for the same wires on the sheet: 数列初值[31:0] = \数列初始值 ; 累加和[31:0] = Result

  // Notes on the sheet:
  //   不要改变此引脚区域内容，也不要改变ALU封装形式
  //   请在下方利用上方输入输出引脚的隧道信号构建等差数列求和电路，ctrl+d复制选择部件
  //   华中科技大学计算机学院 计算机组成原理，鸣谢加州大学伯克利CS61C课程
  //   输出引脚
  //   探测区域
endmodule

// 4位先行进位
module \_4位先行进位加  (
  input  c0,
  input  [3:0] X,
  input  [3:0] Y,
  output [3:0] S,
  output Cf,
  output Cn,
  output G_star,
  output P_star
);

  wire and_2_out, and_3_out, and_4_out, and_5_out, and_6_out, and_7_out, and_8_out, and_9_out, and_10_out,
       and_11_out, C1_out, C2_out;
  wire [3:0] G_out, P_out;

  or or_1 (G_star, and_2_out, and_3_out, and_4_out, G_out[3]);
  and and_1 (P_star, P_out[3], P_out[2], P_out[0], P_out[1]);
  and and_2 (and_2_out, P_out[3], G_out[2]);
  and and_3 (and_3_out, P_out[3], P_out[2], G_out[1]);
  or C4 (Cf, and_2_out, and_3_out, and_4_out, and_5_out, G_out[3]);
  and and_4 (and_4_out, P_out[3], P_out[2], P_out[1], G_out[0]);
  xor xor_1 (S[3], P_out[3], Cn);
  or C3 (Cn, G_out[2], and_6_out, and_7_out, and_8_out);
  and and_5 (and_5_out, P_out[3], P_out[2], P_out[1], P_out[0], c0);
  and and_6 (and_6_out, P_out[2], G_out[1]);
  and and_7 (and_7_out, P_out[2], P_out[1], G_out[0]);
  assign G_out = X & Y;  // AND_Gate G, 4 bits wide
  and and_8 (and_8_out, P_out[2], P_out[1], P_out[0], c0);
  xor xor_2 (S[2], P_out[2], C2_out);
  or C2 (C2_out, G_out[1], and_9_out, and_10_out);
  and and_9 (and_9_out, P_out[1], G_out[0]);
  assign P_out = X ^ Y;  // XOR_Gate P, 4 bits wide
  and and_10 (and_10_out, P_out[1], P_out[0], c0);
  xor xor_3 (S[1], P_out[1], C1_out);
  or C1 (C1_out, G_out[0], and_11_out);
  and and_11 (and_11_out, P_out[0], c0);
  xor xor_4 (S[0], P_out[0], c0);
endmodule

// 16位先行进位
module \_16位先行进位加  (
  input  C0,
  input  [15:0] in_2,
  input  [15:0] in_3,
  output G_star,
  output P_star,
  output C,
  output [15:0] S,
  output Cf,
  output Cn
);

  wire \先行进位器_1_c1 , \先行进位器_1_c2 , \先行进位器_1_c3 ;
  wire [3:0] \n4位先行进位加_4_g_star , \n4位先行进位加_4_p_star ;

  \_4位先行进位加  \u_4位先行进位加_1  (
    .c0(\先行进位器_1_c3 ), .G_star(\n4位先行进位加_4_g_star [3]), .Cf(Cf), .P_star(\n4位先行进位加_4_p_star [3]),
    .X(in_2[15:12]), .Y(in_3[15:12]), .S(S[15:12]), .Cn(Cn));
  \_4位先行进位加  \u_4位先行进位加_2  (
    .c0(\先行进位器_1_c2 ), .G_star(\n4位先行进位加_4_g_star [2]), .P_star(\n4位先行进位加_4_p_star [2]), .X(in_2[11:8]),
    .Y(in_3[11:8]), .S(S[11:8]));  // open: Cf, Cn
  \_4位先行进位加  \u_4位先行进位加_3  (
    .c0(\先行进位器_1_c1 ), .G_star(\n4位先行进位加_4_g_star [1]), .P_star(\n4位先行进位加_4_p_star [1]), .X(in_2[7:4]),
    .Y(in_3[7:4]), .S(S[7:4]));  // open: Cf, Cn
  \先行进位器  \u_先行进位器_1  (
    .G_star(G_star), .P_star(P_star), .c0(C0), .C4(C), .C3(\先行进位器_1_c3 ), .C2(\先行进位器_1_c2 ),
    .C1(\先行进位器_1_c1 ), .G(\n4位先行进位加_4_g_star ), .P(\n4位先行进位加_4_p_star ));
  \_4位先行进位加  \u_4位先行进位加_4  (
    .c0(C0), .G_star(\n4位先行进位加_4_g_star [0]), .P_star(\n4位先行进位加_4_p_star [0]), .X(in_2[3:0]), .Y(in_3[3:0]),
    .S(S[3:0]));  // open: Cf, Cn
endmodule

module \先行进位器  (
  input  c0,
  input  [3:0] G,
  input  [3:0] P,
  output C4,
  output C3,
  output C2,
  output C1,
  output G_star,
  output P_star
);

  wire and_2_out, and_3_out, and_4_out, and_5_out, and_6_out, and_7_out, and_8_out, and_9_out, and_10_out,
       and_11_out;

  or or_1 (G_star, and_2_out, and_3_out, and_4_out, G[3]);
  and and_1 (P_star, P[3], P[2], P[0], P[1]);
  and and_2 (and_2_out, P[3], G[2]);
  and and_3 (and_3_out, P[3], P[2], G[1]);
  or u_C4 (C4, and_2_out, and_3_out, and_4_out, and_5_out, G[3]);
  and and_4 (and_4_out, P[3], P[2], P[1], G[0]);
  or u_C3 (C3, G[2], and_6_out, and_7_out, and_8_out);
  and and_5 (and_5_out, P[3], P[2], P[1], P[0], c0);
  and and_6 (and_6_out, P[2], G[1]);
  and and_7 (and_7_out, P[2], P[1], G[0]);
  and and_8 (and_8_out, P[2], P[1], P[0], c0);
  or u_C2 (C2, G[1], and_9_out, and_10_out);
  and and_9 (and_9_out, P[1], G[0]);
  and and_10 (and_10_out, P[1], P[0], c0);
  or u_C1 (C1, G[0], and_11_out);
  and and_11 (and_11_out, P[0], c0);
endmodule

// C
module \_32位先行进位加法器  (
  input  C0,
  input  [31:0] in_2,
  input  [31:0] in_3,
  output [31:0] S,
  output C
);

  wire and_1_out, C1_out, \n16位先行进位加_2_g_star , \n16位先行进位加_2_p_star ;

  \_16位先行进位加  \u_16位先行进位加_1  (
    .C(C), .S(S[31:16]), .C0(C1_out), .in_2(in_2[31:16]), .in_3(in_3[31:16]));  // open: G_star, P_star, Cf, Cn
  or C1 (C1_out, \n16位先行进位加_2_g_star , and_1_out);
  and and_1 (and_1_out, \n16位先行进位加_2_p_star , C0);
  \_16位先行进位加  \u_16位先行进位加_2  (
    .S(S[15:0]), .C0(C0), .in_2(in_2[15:0]), .in_3(in_3[15:0]), .G_star(\n16位先行进位加_2_g_star ),
    .P_star(\n16位先行进位加_2_p_star ));  // open: C, Cf, Cn
endmodule

module \_32位运算器  (
  input  [31:0] X,
  input  [31:0] Y,
  input  [3:0] ALU_OP,
  output [31:0] Result2,
  output [31:0] Result,
  output OF,
  output UOF,
  output Equal
);

  wire comparator_1_lt, comparator_2_lt;
  wire [1:0] \n32先行进位加减_1_of , \n32先行进位加减_2_of ;
  wire [31:0] and_1_out, bit_extender_1_out, bit_extender_2_out, bit_extender_3_out, bit_extender_4_out,
       divider_1_out, divider_1_rem, multiplier_1_cout, multiplier_1_out, \n32先行进位加减_1_s , \n32先行进位加减_2_s ,
       nor_1_out, or_1_out, shifter_1_out, shifter_2_out, shifter_3_out, xor_1_out;
  wire [31:2] multiplexer_3_out;

  assign bit_extender_1_out = {{30{1'b0}}, \n32先行进位加减_1_of };  // Bit_Extender bit_extender_1
  \_32先行进位加减  \u_32先行进位加减_1  (
    .OF(\n32先行进位加减_1_of [0]), .UOF(\n32先行进位加减_1_of [1]), .X(X), .Y(Y), .S(\n32先行进位加减_1_s ), .C0(1'b0));
  \_32先行进位加减  \u_32先行进位加减_2  (
    .OF(\n32先行进位加减_2_of [0]), .UOF(\n32先行进位加减_2_of [1]), .X(X), .Y(Y), .S(\n32先行进位加减_2_s ), .C0(1'b1));
  assign bit_extender_2_out = {{30{1'b0}}, \n32先行进位加减_2_of };  // Bit_Extender bit_extender_2
  Shifter #(.width(32)) shifter_1 (.in(X), .\dist (Y[4:0]), .out(shifter_1_out));
  Shifter #(.width(32), .shift("ar")) shifter_2 (.in(X), .\dist (Y[4:0]), .out(shifter_2_out));
  Shifter #(.width(32), .shift("lr")) shifter_3 (.in(X), .\dist (Y[4:0]), .out(shifter_3_out));
  Multiplier #(.width(32)) multiplier_1 (
    .a(X), .b(Y), .out(multiplier_1_out), .cin({32{1'b0}}), .cout(multiplier_1_cout));
  Divider #(.width(32)) divider_1 (.a(X), .b(Y), .out(divider_1_out), .upper({32{1'b0}}), .rem(divider_1_rem));
  assign and_1_out = X & Y;  // AND_Gate and_1, 32 bits wide
  assign or_1_out = X | Y;  // OR_Gate or_1, 32 bits wide
  assign xor_1_out = X ^ Y;  // XOR_Gate xor_1, 32 bits wide
  assign nor_1_out = ~(X | Y);  // NOR_Gate nor_1, 32 bits wide
  Comparator #(.width(32)) comparator_1 (.a(X), .b(Y), .eq(Equal), .lt(comparator_1_lt));  // open: gt
  Comparator #(.width(32), .mode("unsigned")) comparator_2 (.a(X), .b(Y), .lt(comparator_2_lt));  // open: gt, eq
  assign bit_extender_3_out = {{31{1'b0}}, comparator_1_lt};  // Bit_Extender bit_extender_3
  assign bit_extender_4_out = {{31{1'b0}}, comparator_2_lt};  // Bit_Extender bit_extender_4
  Multiplexer #(.select(4), .width(32)) multiplexer_1 (
    .in0(shifter_1_out), .in1(shifter_2_out), .in2(shifter_3_out), .in3(multiplier_1_out),
    .in4(divider_1_out), .in5(\n32先行进位加减_1_s ), .in6(\n32先行进位加减_2_s ), .in7(and_1_out), .in8(or_1_out),
    .in9(xor_1_out), .in10(nor_1_out), .in11(bit_extender_3_out), .in12(bit_extender_4_out),
    .in13({32{1'b0}}), .in14({32{1'b0}}), .in15({32{1'b0}}), .out(Result), .sel(ALU_OP), .en(1'b1));
  Multiplexer #(.select(4), .width(32)) multiplexer_2 (
    .in0({32{1'b0}}), .in1({32{1'b0}}), .in2({32{1'b0}}), .in3(multiplier_1_cout), .in4(divider_1_rem),
    .in5({32{1'b0}}), .in6({32{1'b0}}), .in7({32{1'b0}}), .in8({32{1'b0}}), .in9({32{1'b0}}),
    .in10({32{1'b0}}), .in11({32{1'b0}}), .in12({32{1'b0}}), .in13({32{1'b0}}), .in14({32{1'b0}}),
    .in15({32{1'b0}}), .out(Result2), .sel(ALU_OP), .en(1'b1));
  Multiplexer #(.select(4), .width(32)) multiplexer_3 (
    .in0({32{1'b0}}), .in1({32{1'b0}}), .in2({32{1'b0}}), .in3({32{1'b0}}), .in4({32{1'b0}}),
    .in5(bit_extender_1_out), .in6(bit_extender_2_out), .in7({32{1'b0}}), .in8({32{1'b0}}), .in9({32{1'b0}}),
    .in10({32{1'b0}}), .in11({32{1'b0}}), .in12({32{1'b0}}), .in13({32{1'b0}}), .in14({32{1'b0}}),
    .in15({32{1'b0}}), .out({multiplexer_3_out, UOF, OF}), .sel(ALU_OP), .en(1'b1));
endmodule

module \_32先行进位加减  (
  input  C0,
  input  [31:0] X,
  input  [31:0] Y,
  output [31:0] S,
  output OF,
  output UOF
);

  wire and_1_out, C1_out, \n16位先行进位加_1_cf , \n16位先行进位加_1_cn , \n16位先行进位加_2_g_star , \n16位先行进位加_2_p_star ;
  wire [15:0] xor_3_out, xor_3_out_2;
  wire [31:0] bit_extender_1_out;

  xor xor_1 (OF, \n16位先行进位加_1_cf , \n16位先行进位加_1_cn );
  xor xor_2 (UOF, \n16位先行进位加_1_cf , C0);
  \_16位先行进位加  \u_16位先行进位加_1  (
    .S(S[31:16]), .C0(C1_out), .in_2(X[31:16]), .in_3(xor_3_out_2), .Cf(\n16位先行进位加_1_cf ),
    .Cn(\n16位先行进位加_1_cn ));  // open: C, G_star, P_star
  or C1 (C1_out, \n16位先行进位加_2_g_star , and_1_out);
  and and_1 (and_1_out, \n16位先行进位加_2_p_star , C0);
  assign {xor_3_out_2, xor_3_out} = Y ^ bit_extender_1_out;  // XOR_Gate xor_3, 32 bits wide
  \_16位先行进位加  \u_16位先行进位加_2  (
    .S(S[15:0]), .C0(C0), .in_2(X[15:0]), .in_3(xor_3_out), .G_star(\n16位先行进位加_2_g_star ),
    .P_star(\n16位先行进位加_2_p_star ));  // open: C, Cf, Cn
  assign bit_extender_1_out = {{31{C0}}, C0};  // Bit_Extender bit_extender_1
endmodule
