// Logisim project CS1409_U201414816_曾圳_cpu.circ as structural Verilog: 3 circuits, main circuit main
module main (
);

  wire alu_count, alu_src, and_1_out, and_2_out, and_3_out, andi_ori, branch_count, branch_eq, branch_ne,
       clk, clock_1_out, comparator_1_eq, equal, halt, jal, jr, jump, jump_count, mem_count, mem_read,
       mem_reg, mem_write, not_1_out, not_2_out, or_1_out, other_count, reg_dst, reg_write, sll_ra_rl,
       syscall;
  wire [3:0] alu, register_2_q, register_2_q_3, register_2_q_4, register_2_q_5, register_2_q_6,
       register_2_q_7;
  wire [4:0] multiplexer_3_out, multiplexer_4_out;
  wire [9:0] alu_2_result, shifter_3_out;
  wire [11:0] insrtrocture_num_1_alu_num, insrtrocture_num_1_branch_num, insrtrocture_num_1_clk_num,
       insrtrocture_num_1_jump_num, insrtrocture_num_1_mem_num, insrtrocture_num_1_other_num;
  wire [19:4] register_2_q_2;
  wire [21:0] alu_2_result_2;
  wire [31:0] adder_2_out, bit_extender_1_out, bit_extender_2_out, bit_extender_3_out, \mips寄存器组_1_a0 ,
       \mips寄存器组_1_r2 , \mips寄存器组_1_s0 , \mips寄存器组_1_s1 , \mips寄存器组_1_s2 , \mips寄存器组_1_s3 , \mips寄存器组_1_v0 ,
       multiplexer_1_out, multiplexer_5_out, multiplexer_6_out, multiplexer_7_out, multiplexer_8_out,
       multiplexer_9_out, multiplexer_10_out, multiplexer_11_out, multiplexer_12_out, op_4, pc, ram_1_data,
       register_1_q, rom_1_data, shifter_1_out, shifter_2_out;

  Clock clock_1 (.out(clock_1_out));
  Multiplexer #(.width(32), .enable("false")) multiplexer_1 (
    .in0(multiplexer_10_out), .in1(pc), .out(multiplexer_1_out), .sel(jr));
  Register #(.width(32), .trigger("falling")) register_1 (
    .D(multiplexer_1_out), .en(1'b1), .Q(register_1_q), .clk(clk), .clr(1'b0));
  Multiplexer #(.enable("false")) multiplexer_2 (.in0(clock_1_out), .in1(1'b1), .out(clk), .sel(halt));
  insrtrocture_num insrtrocture_num_1 (
    .mem_count(mem_count), .alu_count(alu_count), .jump_count(jump_count), .branch_count(branch_count),
    .mem_num(insrtrocture_num_1_mem_num), .alu_num(insrtrocture_num_1_alu_num),
    .jump_num(insrtrocture_num_1_jump_num), .branch_num(insrtrocture_num_1_branch_num),
    .clk_num(insrtrocture_num_1_clk_num), .clk_count(clk), .other_num(insrtrocture_num_1_other_num),
    .other_count(other_count));
  // Probe on insrtrocture_num_1_jump_num
  // Probe on insrtrocture_num_1_branch_num
  Adder #(.width(32)) adder_1 (.a(register_1_q), .b(32'h1), .out(op_4), .cin(1'b0));  // open: cout
  // Probe on \mips寄存器组_1_s0 
  // Probe on \mips寄存器组_1_s1 
  // Probe on \mips寄存器组_1_s2 
  // Probe on insrtrocture_num_1_mem_num
  // Probe on insrtrocture_num_1_alu_num
  // Probe on insrtrocture_num_1_other_num
  ROM #(.addrWidth(10), .dataWidth(32)) rom_1 (.addr(register_1_q[9:0]), .data(rom_1_data));  // open: sel
  Hex_Digit_Display hex_digit_display_1 (.value(register_2_q_7));  // open: dp
  // Probe on insrtrocture_num_1_clk_num
  Hex_Digit_Display hex_digit_display_2 (.value(register_2_q_5));  // open: dp
  Hex_Digit_Display hex_digit_display_3 (.value(register_2_q_6));  // open: dp
  Multiplexer #(.width(5), .enable("false")) multiplexer_3 (
    .in0(rom_1_data[20:16]), .in1(rom_1_data[15:11]), .out(multiplexer_3_out), .sel(reg_dst));
  assign bit_extender_1_out = {{16{rom_1_data[15]}}, rom_1_data[15:0]};  // Bit_Extender bit_extender_1
  assign bit_extender_2_out = {{16{1'b0}}, rom_1_data[15:0]};  // Bit_Extender bit_extender_2
  Hex_Digit_Display hex_digit_display_4 (.value(register_2_q_2[19:16]));  // open: dp
  Shifter #(.width(32)) shifter_1 (.in(rom_1_data), .\dist ({5{1'b0}}), .out(shifter_1_out));
  Multiplexer #(.width(5), .enable("false")) multiplexer_4 (
    .in0(multiplexer_3_out), .in1({5{1'b1}}), .out(multiplexer_4_out), .sel(jal));
  Multiplexer #(.width(32), .enable("false")) multiplexer_5 (
    .in0(bit_extender_1_out), .in1(bit_extender_2_out), .out(multiplexer_5_out), .sel(andi_ori));
  assign bit_extender_3_out = {{27{1'b0}}, rom_1_data[10:6]};  // Bit_Extender bit_extender_3
  Hex_Digit_Display hex_digit_display_5 (.value(register_2_q_3));  // open: dp
  Hex_Digit_Display hex_digit_display_6 (.value(register_2_q_4));  // open: dp
  Shifter #(.width(32)) shifter_2 (.in(multiplexer_5_out), .\dist ({5{1'b0}}), .out(shifter_2_out));
  // Probe on \mips寄存器组_1_s3 
  Hex_Digit_Display hex_digit_display_7 (.value(register_2_q_2[7:4]));  // open: dp
  Adder #(.width(32)) adder_2 (.a(op_4), .b(shifter_2_out), .out(adder_2_out), .cin(1'b0));  // open: cout
  \控制电路改进  \u_控制电路改进_1  (
    .op(rom_1_data[31:26]), .func(rom_1_data[5:0]), .alu_op(alu), .reg_dst(reg_dst), .branch_ne(branch_ne),
    .jump(jump), .reg_write(reg_write), .mem_read(mem_read), .mem_write(mem_write), .alu_src(alu_src),
    .mem_reg(mem_reg), .syacall(syscall), .branch_eq(branch_eq), .jr(jr), .jal(jal), .sll_ra(sll_ra_rl),
    .andi_ori(andi_ori), .alu_count(alu_count), .jump_count(jump_count), .branch_count(branch_count),
    .mem_count(mem_count), .other_count(other_count));
  Hex_Digit_Display hex_digit_display_8 (.value(register_2_q));  // open: dp
  Multiplexer #(.width(32), .enable("false")) multiplexer_6 (
    .in0(pc), .in1(\mips寄存器组_1_r2 ), .out(multiplexer_6_out), .sel(sll_ra_rl));
  \MIPS寄存器组  \mips寄存器组_1  (
    .W_num(multiplexer_4_out), .Din(multiplexer_11_out), .WE(reg_write), .R2_num(rom_1_data[20:16]),
    .R1_num(rom_1_data[25:21]), .s0(\mips寄存器组_1_s0 ), .s1(\mips寄存器组_1_s1 ), .s2(\mips寄存器组_1_s2 ), .R1(pc),
    .R2(\mips寄存器组_1_r2 ), .clk(clk), .v0(\mips寄存器组_1_v0 ), .s3(\mips寄存器组_1_s3 ), .a0(\mips寄存器组_1_a0 ));  // open: ra, s4
  Multiplexer #(.width(32), .enable("false")) multiplexer_7 (
    .in0(\mips寄存器组_1_r2 ), .in1(multiplexer_5_out), .out(multiplexer_7_out), .sel(alu_src));
  Multiplexer #(.width(32), .enable("false")) multiplexer_8 (
    .in0(op_4), .in1(adder_2_out), .out(multiplexer_8_out), .sel(or_1_out));
  Multiplexer #(.width(32), .enable("false")) multiplexer_9 (
    .in0(multiplexer_7_out), .in1(bit_extender_3_out), .out(multiplexer_9_out), .sel(sll_ra_rl));
  Register #(.width(32), .trigger("falling")) register_2 (
    .D(\mips寄存器组_1_a0 ), .en(and_1_out),
    .Q({register_2_q_7, register_2_q_6, register_2_q_5, register_2_q_2[19:16], register_2_q_4, register_2_q_3, register_2_q_2[7:4], register_2_q}),
    .clk(clk), .clr(1'b0));
  Multiplexer #(.width(32), .enable("false")) multiplexer_10 (
    .in0(multiplexer_8_out), .in1({op_4[31:28], shifter_1_out[27:0]}), .out(multiplexer_10_out), .sel(jump));
  ALU alu_2 (
    .AluOP(alu), .X(multiplexer_6_out), .Equal(equal), .Result({alu_2_result_2, alu_2_result}),
    .Y(multiplexer_9_out));  // open: Signed_Overflow, Result_2, UnSigned_Overflow
  or or_1 (or_1_out, and_3_out, and_2_out);
  Shifter #(.width(10), .shift("ar")) shifter_3 (.in(alu_2_result), .\dist (4'b0010), .out(shifter_3_out));
  and and_1 (and_1_out, syscall, not_1_out);
  and and_2 (and_2_out, not_2_out, branch_ne);
  Comparator #(.width(32)) comparator_1 (.a(32'ha), .b(\mips寄存器组_1_v0 ), .eq(comparator_1_eq));  // open: gt, lt
  not not_1 (not_1_out, halt);
  and and_3 (and_3_out, equal, branch_eq);
  not not_2 (not_2_out, equal);
  and and_4 (halt, syscall, comparator_1_eq);
  RAM #(.addrWidth(10), .dataWidth(32), .bus("separate")) ram_1 (
    .addr(shifter_3_out), .din(\mips寄存器组_1_r2 ), .data(ram_1_data), .str(mem_write), .sel(1'b1), .clk(clk),
    .ld(mem_read), .clr(1'b0));
  Multiplexer #(.width(32), .enable("false")) multiplexer_11 (
    .in0(multiplexer_12_out), .in1(op_4), .out(multiplexer_11_out), .sel(jal));
  Multiplexer #(.width(32), .enable("false")) multiplexer_12 (
    .in0(ram_1_data), .in1({alu_2_result_2, alu_2_result}), .out(multiplexer_12_out), .sel(mem_reg));

  // Notes on the sheet:
  //   contents of rom_1 (hex, n*v repeats v):
  //   20110001 8000c05 20110001 20120002 20130003 8000c09 20110001 20120002 20130003 8000c0d 20110001
  //   20120002 20130003 8000c11 20110001 20120002 20130003 c000cb8 20100001 20110001 118fc0 112020
  //   20020022 c 118882 12200001 8000c15 112020 20020022 c 20110001 118880 112020 20020022 c 12200001
  //   8000c1f 20110001 118fc0 112020 20020022 c 1188c3 112020 20020022 c 118903 112020 20020022 c 118903
  //   112020 20020022 c 118903 112020 20020022 c 118903 112020 20020022 c 118903 112020 20020022 c 118903
  //   112020 20020022 c 118903 112020 20020022 c 20100001 109fc0 139fc3 8021 2012000c 24160003 26100001
  //   3210000f 20080008 20090001 139900 2709825 132020 20020022 c 1094022 1500fff9 22100001 2018000f
  //   2188024 108700 20080008 20090001 139902 2709825 132021 20020022 c 1094022 1500fff9 108702 2c9b022
  //   12c00001 8000c50 4020 1084027 84400 3508ffff 82021 20020022 c 2010ffff 20110000 ae300000 22100001
  //   22310004 ae300000 22100001 22310004 ae300000 22100001 22310004 ae300000 22100001 22310004 ae300000
  //   22100001 22310004 ae300000 22100001 22310004 ae300000 22100001 22310004 ae300000 22100001 22310004
  //   ae300000 22100001 22310004 ae300000 22100001 22310004 ae300000 22100001 22310004 ae300000 22100001
  //   22310004 ae300000 22100001 22310004 ae300000 22100001 22310004 ae300000 22100001 22310004 ae300000
  //   22100001 22310004 22100001 8020 2011003c 8e130000 8e340000 274402a 11000002 ae330000 ae140000
  //   2231fffc 1611fff8 102020 20020022 c 22100004 2011003c 1611fff2 2002000a c 20100000 22100001 102020
  //   20020022 c 22100002 102020 20020022 c 22100003 102020 20020022 c 22100004 102020 20020022 c 22100005
  //   102020 20020022 c 22100006 102020 20020022 c 22100007 102020 20020022 c 22100008 102020 20020022
  //   20020022 c 3e00008
endmodule

// 控制单元
module \控制电路改进  (
  input  [5:0] op,
  input  [5:0] func,
  output branch_eq,
  output reg_dst,
  output branch_ne,
  output jump,
  output mem_read,
  output mem_write,
  output alu_src,
  output syacall,
  output jr,
  output jal,
  output sll_ra,
  output andi_ori,
  output alu_count,
  output jump_count,
  output branch_count,
  output mem_count,
  output other_count,
  output reg_write,
  output mem_reg,
  output [3:0] alu_op
);

  wire add, addi, addiu, addu, \and , andi, j, mem_reg_3_out, mem_reg_out, \nor , op_t, \or , or_1_out,
       or_2_out, or_4_out, ori, reg_write_3_out, reg_write_out, sll, slt, slti, sltu, sra, srl, sub;
  wire [3:0] and_1_out, and_2_out, and_3_out, and_4_out, and_5_out, and_6_out, and_7_out, and_9_out,
       and_10_out, and_11_out, and_12_out, and_13_out, bit_extender_1_out, bit_extender_2_out,
       bit_extender_3_out, bit_extender_4_out, bit_extender_5_out, bit_extender_6_out, bit_extender_7_out,
       bit_extender_8_out, bit_extender_9_out, bit_extender_10_out, bit_extender_11_out, bit_extender_12_out,
       or_3_out, or_6_out;
  wire [5:0] not_1_out, not_2_out;

  assign not_1_out = ~op;  // NOT_Gate not_1, 6 bits wide
  assign not_2_out = ~func;  // NOT_Gate not_2, 6 bits wide
  and u_op (op_t, not_1_out[0], not_1_out[1], not_1_out[2], not_1_out[3], not_1_out[4], not_1_out[5]);
  and u_add (add, not_2_out[4], not_2_out[3], not_2_out[2], not_2_out[1], not_2_out[0], func[5], op_t);
  or u_reg_dst (reg_dst, add, addu, \and , sll, sra, srl, sub, \or , \nor , slt, sltu);
  or or_1 (or_1_out, add, addiu, addi, mem_write, mem_read);
  assign bit_extender_1_out = {{3{or_1_out}}, or_1_out};  // Bit_Extender bit_extender_1
  assign bit_extender_2_out = {{3{addu}}, addu};  // Bit_Extender bit_extender_2
  or or_2 (or_2_out, \and , andi);
  assign bit_extender_3_out = {{3{or_2_out}}, or_2_out};  // Bit_Extender bit_extender_3
  assign bit_extender_4_out = {{3{sll}}, sll};  // Bit_Extender bit_extender_4
  and lw (mem_read, op[0], op[1], op[5], not_1_out[2], not_1_out[3], not_1_out[4]);
  and u_addi (addi, op[3], not_1_out[0], not_1_out[1], not_1_out[2], not_1_out[4], not_1_out[5]);
  assign and_1_out = bit_extender_1_out & 4'b0101;  // AND_Gate and_1, 4 bits wide
  assign and_2_out = bit_extender_2_out & 4'b0101;  // AND_Gate and_2, 4 bits wide
  assign and_3_out = bit_extender_3_out & 4'b0111;  // AND_Gate and_3, 4 bits wide
  assign and_4_out = bit_extender_4_out & 4'b0000;  // AND_Gate and_4, 4 bits wide
  and sw (mem_write, op[0], op[1], op[3], op[5], not_1_out[2], not_1_out[4]);
  and u_addiu (addiu, op[0], op[3], not_1_out[1], not_1_out[2], not_1_out[4], not_1_out[5]);
  or u_jump (jump, jr, jal, j);
  assign bit_extender_5_out = {{3{sra}}, sra};  // Bit_Extender bit_extender_5
  assign bit_extender_6_out = {{3{srl}}, srl};  // Bit_Extender bit_extender_6
  assign bit_extender_7_out = {{3{\nor }}, \nor };  // Bit_Extender bit_extender_7
  and beq (branch_eq, op[2], not_1_out[0], not_1_out[1], not_1_out[3], not_1_out[4], not_1_out[5]);
  and u_addu (addu, func[0], func[5], not_2_out[1], not_2_out[2], not_2_out[3], not_2_out[4], op_t);
  assign and_5_out = bit_extender_5_out & 4'b0001;  // AND_Gate and_5, 4 bits wide
  assign and_6_out = bit_extender_6_out & 4'b0010;  // AND_Gate and_6, 4 bits wide
  assign and_7_out = bit_extender_7_out & 4'b1010;  // AND_Gate and_7, 4 bits wide
  and and_8 (\and , func[2], func[5], not_2_out[0], not_2_out[1], not_2_out[3], not_2_out[4], op_t);
  or u_reg_write (reg_write_out, add, addu, \and , sll, sra, srl, sub, \or , \nor , slt, sltu);
  or reg_write_2 (reg_write, reg_write_out, reg_write_3_out);
  and bne (branch_ne, op[0], op[2], not_1_out[1], not_1_out[3], not_1_out[4], not_1_out[5]);
  and u_andi (andi, op[2], op[3], not_1_out[0], not_1_out[1], not_1_out[4], not_1_out[5]);
  or reg_write_3 (reg_write_3_out, ori, andi, addi, jal, addiu, slti, mem_read);
  assign or_3_out = and_1_out | and_5_out | and_2_out | and_6_out | and_3_out | and_7_out | and_4_out;  // OR_Gate or_3, 4 bits wide
  or or_4 (or_4_out, slt, slti);
  and u_slti (slti, op[1], op[3], not_1_out[0], not_1_out[2], not_1_out[4], not_1_out[5]);
  and u_sll (sll, not_2_out[0], not_2_out[1], not_2_out[2], not_2_out[3], not_2_out[4], not_2_out[5], op_t);
  assign bit_extender_8_out = {{3{sltu}}, sltu};  // Bit_Extender bit_extender_8
  assign bit_extender_9_out = {{3{or_4_out}}, or_4_out};  // Bit_Extender bit_extender_9
  and u_j (j, op[1], not_1_out[0], not_1_out[2], not_1_out[3], not_1_out[4], not_1_out[5]);
  and u_sra (sra, func[0], func[1], not_2_out[2], not_2_out[3], not_2_out[4], not_2_out[5], op_t);
  assign and_9_out = bit_extender_8_out & 4'b1100;  // AND_Gate and_9, 4 bits wide
  assign and_10_out = bit_extender_9_out & 4'b1011;  // AND_Gate and_10, 4 bits wide
  and u_jal (jal, op[0], op[1], not_1_out[2], not_1_out[3], not_1_out[4], not_1_out[5]);
  and u_srl (srl, func[1], not_2_out[0], not_2_out[2], not_2_out[3], not_2_out[4], not_2_out[5], op_t);
  assign bit_extender_10_out = {{3{sub}}, sub};  // Bit_Extender bit_extender_10
  assign bit_extender_11_out = {{3{ori}}, ori};  // Bit_Extender bit_extender_11
  assign bit_extender_12_out = {{3{\or }}, \or };  // Bit_Extender bit_extender_12
  and u_sub (sub, func[1], func[5], not_2_out[0], not_2_out[2], not_2_out[3], not_2_out[4], op_t);
  or u_alu_src (alu_src, ori, andi, addi, mem_read, addiu, slti, mem_write);
  assign and_11_out = bit_extender_10_out & 4'b0110;  // AND_Gate and_11, 4 bits wide
  assign and_12_out = bit_extender_11_out & 4'b1000;  // AND_Gate and_12, 4 bits wide
  assign and_13_out = bit_extender_12_out & 4'b1000;  // AND_Gate and_13, 4 bits wide
  and or_5 (\or , func[0], func[2], func[5], not_2_out[1], not_2_out[3], not_2_out[4], op_t);
  or u_mem_reg (mem_reg_out, add, addu, \and , sll, sra, srl, sub, \or , \nor , slt, sltu);
  and u_ori (ori, op[0], op[2], op[3], not_1_out[1], not_1_out[4], not_1_out[5]);
  or mem_reg_2 (mem_reg, mem_reg_out, mem_reg_3_out);
  assign or_6_out = and_9_out | and_11_out | and_12_out | and_13_out | and_10_out;  // OR_Gate or_6, 4 bits wide
  and u_nor (\nor , func[0], func[1], func[2], func[5], not_2_out[3], not_2_out[4], op_t);
  or mem_reg_3 (mem_reg_3_out, ori, andi, addi, addiu, slti);
  assign alu_op = or_3_out | or_6_out;  // OR_Gate or_7, 4 bits wide
  and u_slt (slt, func[1], func[3], func[5], not_2_out[0], not_2_out[2], not_2_out[4], op_t);
  and u_sltu (sltu, func[0], func[1], func[3], func[5], not_2_out[2], not_2_out[4], op_t);
  and u_jr (jr, func[3], not_2_out[0], not_2_out[1], not_2_out[2], not_2_out[4], not_2_out[5], op_t);
  and syscall (syacall, func[2], func[3], not_2_out[0], not_2_out[1], not_2_out[4], not_2_out[5], op_t);
  or u_sll_ra (sll_ra, sll, srl, sra);
  or u_andi_ori (andi_ori, andi, ori);
  or u_alu_count (alu_count, add, \and , sll, sra, srl, sub, \or , \nor , ori, andi, addi, addiu, slti);
  or u_jump_count (jump_count, jr, jal, j);
  or u_branch_count (branch_count, branch_eq, branch_ne);
  or u_mem_count (mem_count, mem_read, mem_write);
  or u_other_count (other_count, sltu, slt, syacall, addu);

  // Other names for the same wires on the sheet: beq = branch_eq; bne = branch_ne; lw = mem_read; sw = mem_write;
  //   syscall = syacall
endmodule

module insrtrocture_num (
  input  mem_count,
  input  alu_count,
  input  jump_count,
  input  branch_count,
  input  clk_count,
  input  other_count,
  output [11:0] mem_num,
  output [11:0] alu_num,
  output [11:0] jump_num,
  output [11:0] branch_num,
  output [11:0] clk_num,
  output [11:0] other_num
);

  wire [11:0] adder_1_out, adder_2_out, adder_3_out, adder_4_out, adder_5_out, adder_6_out;

  Register #(.width(12)) register_1 (.D(adder_1_out), .en(mem_count), .Q(mem_num), .clk(clk_count), .clr(1'b0));
  Register #(.width(12)) register_2 (.D(adder_2_out), .en(alu_count), .Q(alu_num), .clk(clk_count), .clr(1'b0));
  Register #(.width(12)) register_3 (.D(adder_3_out), .en(jump_count), .Q(jump_num), .clk(clk_count), .clr(1'b0));
  Register #(.width(12)) register_4 (.D(adder_4_out), .en(branch_count), .Q(branch_num), .clk(clk_count), .clr(1'b0));
  Register #(.width(12)) register_5 (.D(adder_5_out), .en(1'b1), .Q(clk_num), .clk(clk_count), .clr(1'b0));
  Register #(.width(12)) register_6 (.D(adder_6_out), .en(other_count), .Q(other_num), .clk(clk_count), .clr(1'b0));
  Adder #(.width(12)) adder_1 (.a(mem_num), .b(12'h1), .out(adder_1_out), .cin(1'b0));  // open: cout
  Adder #(.width(12)) adder_2 (.a(alu_num), .b(12'h1), .out(adder_2_out), .cin(1'b0));  // open: cout
  Adder #(.width(12)) adder_3 (.a(jump_num), .b(12'h1), .out(adder_3_out), .cin(1'b0));  // open: cout
  Adder #(.width(12)) adder_4 (.a(branch_num), .b(12'h1), .out(adder_4_out), .cin(1'b0));  // open: cout
  Adder #(.width(12)) adder_5 (.a(clk_num), .b(12'h1), .out(adder_5_out), .cin(1'b0));  // open: cout
  Adder #(.width(12)) adder_6 (.a(other_num), .b(12'h1), .out(adder_6_out), .cin(1'b0));  // open: cout
endmodule
