// Logisim project regfile-test.circ as structural Verilog: 1 circuit, main circuit main
module main (
  output [7:0] test_num,
  output [31:0] Reg_0_Value,
  output [31:0] Reg_1_Value,
  output [31:0] Reg_2_Value,
  output [31:0] Reg_3_Value,
  output [31:0] Read_Data_1,
  output [31:0] Read_Data_2
);

  wire clock_1_out;
  wire [7:0] adder_1_out;
  wire [15:0] rom_2_data;
  wire [31:0] WriteData;

  Register register_1 (.D(adder_1_out), .en(1'b1), .Q(test_num), .clk(clock_1_out));  // open: clr
  Adder adder_1 (.a(8'h1), .b(test_num), .out(adder_1_out));  // open: cin, cout
  ROM #(.dataWidth(32)) rom_1 (.addr(test_num), .data(WriteData));  // open: sel
  ROM #(.dataWidth(16)) rom_2 (.addr(test_num), .data(rom_2_data), .sel(1'b1));
  // Probe on rom_2_data[4:0]
  // Probe on rom_2_data[14:10]
  // Probe on rom_2_data[9:5]
  Clock clock_1 (.out(clock_1_out));
  // regfile_main main_1: pin names not known; wires that end beside it: rom_2_data[4:0], rom_2_data[9:5], rom_2_data[14:10], Reg_0_Value, WriteData, Reg_1_Value, rom_2_data[15], Reg_2_Value, clock_1_out, Reg_3_Value, Read_Data_1, Read_Data_2

  // Notes on the sheet:
  //   contents of rom_1 (hex, n*v repeats v):
  //   1 2 3 4 5 6 7 8 9 a b c d e f 10 11 12 13 14 15 16 17 18 19 1a 1b 1c 1d 1e 1f 20
  //   contents of rom_2 (hex, n*v repeats v):
  //   8441 8841 8c41 9441 9841 9c41 a041
  //   图中不应该有蓝色或红色线缆，也不应该出现未知状态 x.
  //   你的寄存器文件封装正好合适放在这里
endmodule
